// Logisim project HEX-DEC-converter.circ as structural Verilog: 7 circuits, main circuit main
module main (
);

  wire _0, _1, _2, _3, _4, _5, _6, _7, _8, _9, A, B, C, D, DELETE, E, F;
  wire [2:0] _1_B, _2_B, _3_B;
  wire [3:0] _1_T, _2_T, _3_T, First, Second;

  Hex_Digit_Display hex_digit_display_1 (.value(Second));  // open: dp
  Hex_Digit_Display hex_digit_display_2 (.value(First));  // open: dp
  _7_Segment_Display u_7_segment_display_1 (
    .g(_1_T[3]), .f(_1_T[2]), .a(_1_T[1]), .b(_1_T[0]), .e(_1_B[2]), .d(_1_B[1]), .c(_1_B[0]));  // open: dp
  _7_Segment_Display u_7_segment_display_2 (
    .g(_2_T[3]), .f(_2_T[2]), .a(_2_T[1]), .b(_2_T[0]), .e(_2_B[2]), .d(_2_B[1]), .c(_2_B[0]));  // open: dp
  Button u__0 (.out(_0));
  Button u__8 (.out(_8));
  Button u__1 (.out(_1));
  Button u__9 (.out(_9));
  Button u__2 (.out(_2));
  Button u_A (.out(A));
  Button u_B (.out(B));
  Button u__3 (.out(_3));
  Button u_C (.out(C));
  Button u__4 (.out(_4));
  Button u__5 (.out(_5));
  Button u_D (.out(D));
  Button u_E (.out(E));
  Button u__6 (.out(_6));
  Button u__7 (.out(_7));
  Button u_F (.out(F));
  Button button_1 (.out(DELETE));
  _7_Segment_Display u_7_segment_display_3 (
    .g(_3_T[3]), .f(_3_T[2]), .a(_3_T[1]), .b(_3_T[0]), .e(_3_B[2]), .d(_3_B[1]), .c(_3_B[0]));  // open: dp
  Convertor convertor_1 (
    ._3_Top(_3_T), ._3_Bottom(_3_B), ._2_Top(_2_T), ._2_Bottom(_2_B), ._1_Top(_1_T), ._1_Bottom(_1_B),
    .First_number(First), .Second_number(Second), ._0(_0), ._1(_1), ._2(_2), ._3(_3), ._4(_4), ._5(_5),
    ._6(_6), ._7(_7), ._8(_8), ._9(_9), .A(A), .B(B), .C(C), .D(D), .E(E), .F(F), .Delete(DELETE));

  // Notes on the sheet:
  //   HEX
  //   DEC
  //   Klávesnice
  //   Převod
  //   Pomocí žlutých tlačítek zadejte číslo v HEX podobě.
  //   Pro smazání displeje stiskněte červené tlačítko DELETE
  //   Číslo z HEX displeje se vám zobrazí převedené na DEC displeji.
endmodule

// Display 3
module _3_Display (
  input  A,
  input  B,
  input  C,
  input  D,
  input  E,
  input  F,
  input  G,
  input  H,
  output Top,
  output Middle,
  output Bottom,
  output LeftTop,
  output LeftBottom,
  output RightTop,
  output RightBottom
);

  wire and_1_out, and_2_out, and_3_out, and_4_out, and_5_out, and_6_out, and_7_out, and_8_out, and_9_out,
       and_10_out, and_11_out, and_12_out, and_13_out, and_14_out, and_15_out, and_16_out, and_17_out,
       and_18_out, and_19_out, and_20_out, and_21_out, and_22_out, and_23_out, and_24_out, and_25_out,
       and_26_out, and_27_out, and_28_out, and_29_out, and_30_out, and_31_out, and_32_out, and_33_out,
       and_34_out, and_35_out, and_36_out, and_37_out, and_38_out, and_39_out, and_40_out, and_41_out,
       and_42_out, and_43_out, and_44_out, and_45_out, and_46_out, and_47_out, and_48_out, and_49_out,
       and_50_out, and_51_out, and_52_out, and_53_out, and_54_out, and_55_out, and_56_out, and_57_out,
       and_58_out, and_59_out, and_60_out, and_61_out, and_62_out, and_63_out, and_64_out, and_65_out,
       and_66_out, and_67_out, and_68_out, and_69_out, and_70_out, and_71_out, and_72_out, and_73_out,
       and_74_out, and_75_out, and_76_out, and_77_out, and_78_out, and_79_out, and_80_out, and_81_out,
       and_82_out, and_83_out, and_84_out, and_85_out, and_86_out, and_87_out, and_88_out, and_89_out,
       and_90_out, and_91_out, and_92_out, and_93_out, and_94_out, and_95_out, and_96_out, and_97_out,
       and_98_out, and_99_out, and_100_out, and_101_out, and_102_out, and_103_out, and_104_out, and_105_out,
       and_106_out, and_107_out, and_108_out, and_109_out, and_110_out, and_111_out, and_112_out,
       and_113_out, and_114_out, and_115_out, and_116_out, and_117_out, and_118_out, and_119_out,
       and_120_out, and_121_out, and_122_out, and_123_out, and_124_out, and_125_out, and_126_out,
       and_127_out, and_128_out, and_129_out, and_130_out, and_131_out, and_132_out, and_133_out,
       and_134_out, and_135_out, and_136_out, and_137_out, and_138_out, and_139_out, and_140_out,
       and_141_out, and_142_out, and_143_out, and_144_out, and_145_out, and_146_out, and_147_out,
       and_148_out, and_149_out, and_150_out, and_151_out, and_152_out, and_153_out, and_154_out,
       and_155_out, and_156_out, and_157_out, and_158_out, and_159_out, and_160_out, and_161_out,
       and_162_out, and_163_out, and_164_out, and_165_out, and_166_out, and_167_out, and_168_out,
       and_169_out, and_170_out, and_171_out, and_172_out, and_173_out, and_174_out, and_175_out,
       and_176_out, and_177_out, and_178_out, and_179_out, and_180_out, and_181_out, and_182_out,
       and_183_out, and_184_out, and_185_out, and_186_out, and_187_out, and_188_out, and_189_out,
       and_190_out, and_191_out, and_192_out, and_193_out, and_194_out, and_195_out, and_196_out,
       and_197_out, and_198_out, and_199_out, and_200_out, and_201_out, and_202_out, and_203_out,
       and_204_out, and_205_out, and_206_out, and_207_out, and_208_out, and_209_out, and_210_out,
       and_211_out, and_212_out, and_213_out, and_214_out, and_215_out, and_216_out, and_217_out,
       and_218_out, and_219_out, and_220_out, and_221_out, and_222_out, and_223_out, and_224_out,
       and_225_out, and_226_out, and_227_out, and_228_out, and_229_out, and_230_out, and_231_out,
       and_232_out, and_233_out, and_234_out, and_235_out, and_236_out, and_237_out, and_238_out,
       and_239_out, and_240_out, and_241_out, and_242_out, and_243_out, and_244_out, and_245_out,
       and_246_out, and_247_out, and_248_out, and_249_out, and_250_out, and_251_out, and_252_out,
       and_253_out, and_254_out, and_255_out, and_256_out, and_257_out, and_258_out, and_259_out,
       and_260_out, and_261_out, and_262_out, and_263_out, and_264_out, and_265_out, and_266_out,
       and_267_out, and_268_out, and_269_out, and_270_out, and_271_out, and_272_out, and_273_out,
       and_274_out, and_275_out, and_276_out, and_277_out, and_278_out, and_279_out, and_280_out,
       and_281_out, and_282_out, and_283_out, and_284_out, and_285_out, and_286_out, and_287_out,
       and_288_out, and_289_out, and_290_out, and_291_out, and_292_out, and_293_out, and_294_out,
       and_295_out, and_296_out, and_297_out, and_298_out, and_299_out, and_300_out, and_301_out,
       and_302_out, and_303_out, and_304_out, and_305_out, and_306_out, and_307_out, and_308_out,
       and_309_out, and_310_out, and_311_out, and_312_out, and_313_out, and_314_out, and_315_out,
       and_316_out, and_317_out, and_318_out, and_319_out, and_320_out, and_321_out, and_322_out,
       and_323_out, and_324_out, and_325_out, and_326_out, and_327_out, and_328_out, and_329_out,
       and_330_out, and_331_out, and_332_out, and_333_out, and_334_out, and_335_out, and_336_out,
       and_337_out, and_338_out, and_339_out, and_340_out, and_341_out, and_342_out, and_343_out,
       and_344_out, and_345_out, and_346_out, and_347_out, and_348_out, and_349_out, and_350_out,
       and_351_out, and_352_out, and_353_out, and_354_out, and_355_out, and_356_out, and_357_out,
       and_358_out, and_359_out, and_360_out, and_361_out, and_362_out, and_363_out, and_364_out,
       and_365_out, and_366_out, and_367_out, and_368_out, and_369_out, and_370_out, and_371_out,
       and_372_out, and_373_out, and_374_out, and_375_out, not_1_out, not_2_out, not_3_out, not_4_out,
       not_5_out, not_6_out, not_7_out, not_8_out, not_9_out, not_10_out, not_11_out, not_12_out, not_13_out,
       not_14_out, not_15_out, not_16_out, not_17_out, not_18_out, not_19_out, not_20_out, not_21_out,
       not_22_out, not_23_out, not_24_out, not_25_out, not_26_out, not_27_out, not_28_out, not_29_out,
       not_30_out, not_31_out, not_32_out, not_33_out, not_34_out, not_35_out, not_36_out, not_37_out,
       not_38_out, not_39_out, not_40_out, not_41_out, not_42_out, not_43_out, not_44_out, not_45_out,
       not_46_out, not_47_out, not_48_out, not_49_out, not_50_out, not_51_out, not_52_out, not_53_out,
       not_54_out, not_55_out, not_56_out, not_57_out, not_58_out, not_59_out, not_60_out, not_61_out,
       not_62_out, not_63_out, not_64_out, not_65_out, not_66_out, not_67_out, not_68_out, not_69_out,
       not_70_out, not_71_out, not_72_out, not_73_out, not_74_out, not_75_out, not_76_out, not_77_out,
       not_78_out, not_79_out, not_80_out, not_81_out, not_82_out, not_83_out, not_84_out, not_85_out,
       not_86_out, not_87_out, not_88_out, not_89_out, not_90_out, not_91_out, not_92_out, not_93_out,
       not_94_out, not_95_out, not_96_out, not_97_out, not_98_out, not_99_out, not_100_out, not_101_out,
       not_102_out, not_103_out, not_104_out, not_105_out, not_106_out, not_107_out, not_108_out,
       not_109_out, not_110_out, not_111_out, not_112_out, not_113_out, not_114_out, not_115_out,
       not_116_out, not_117_out, not_118_out, not_119_out, not_120_out, not_121_out, not_122_out,
       not_123_out, not_124_out, not_125_out, not_126_out, not_127_out, not_128_out, not_129_out,
       not_130_out, not_131_out, not_132_out, not_133_out, not_134_out, not_135_out, not_136_out,
       not_137_out, not_138_out, not_139_out, not_140_out, not_141_out, not_142_out, not_143_out,
       not_144_out, not_145_out, not_146_out, not_147_out, not_148_out, not_149_out, not_150_out,
       not_151_out, not_152_out, not_153_out, not_154_out, not_155_out, not_156_out, not_157_out,
       not_158_out, not_159_out, not_160_out, not_161_out, not_162_out, not_163_out, not_164_out,
       not_165_out, not_166_out, not_167_out, not_168_out, not_169_out, not_170_out, not_171_out,
       not_172_out, not_173_out, not_174_out, not_175_out, not_176_out, not_177_out, not_178_out,
       not_179_out, not_180_out, not_181_out, not_182_out, not_183_out, not_184_out, not_185_out,
       not_186_out, not_187_out, not_188_out, not_189_out, not_190_out, not_191_out, not_192_out,
       not_193_out, not_194_out, not_195_out, not_196_out, not_197_out, not_198_out, not_199_out,
       not_200_out, not_201_out, not_202_out, not_203_out, not_204_out, not_205_out, not_206_out,
       not_207_out, not_208_out, not_209_out, not_210_out, not_211_out, not_212_out, not_213_out,
       not_214_out, not_215_out, not_216_out, not_217_out, not_218_out, not_219_out, not_220_out,
       not_221_out, not_222_out, not_223_out, not_224_out, not_225_out, not_226_out, not_227_out,
       not_228_out, not_229_out, not_230_out, not_231_out, not_232_out, not_233_out, not_234_out,
       not_235_out, not_236_out, not_237_out, not_238_out, not_239_out, not_240_out, not_241_out,
       not_242_out, not_243_out, not_244_out, not_245_out, not_246_out, not_247_out, not_248_out,
       not_249_out, not_250_out, not_251_out, not_252_out, not_253_out, not_254_out, not_255_out,
       not_256_out, not_257_out, not_258_out, not_259_out, not_260_out, not_261_out, not_262_out,
       not_263_out, not_264_out, not_265_out, not_266_out, not_267_out, not_268_out, not_269_out,
       not_270_out, not_271_out, not_272_out, not_273_out, not_274_out, not_275_out, not_276_out,
       not_277_out, not_278_out, not_279_out, not_280_out, not_281_out, not_282_out, not_283_out,
       not_284_out, not_285_out, not_286_out, not_287_out, not_288_out, not_289_out, not_290_out,
       not_291_out, not_292_out, not_293_out, not_294_out, not_295_out, not_296_out, not_297_out,
       not_298_out, not_299_out, not_300_out, not_301_out, not_302_out, not_303_out, not_304_out,
       not_305_out, not_306_out, not_307_out, not_308_out, not_309_out, not_310_out, not_311_out,
       not_312_out, not_313_out, not_314_out, not_315_out, not_316_out, not_317_out, not_318_out,
       not_319_out, not_320_out, not_321_out, not_322_out, not_323_out, not_324_out, not_325_out,
       not_326_out, not_327_out, not_328_out, not_329_out, not_330_out, not_331_out, not_332_out,
       not_333_out, not_334_out, not_335_out, not_336_out, not_337_out, not_338_out, not_339_out,
       not_340_out, not_341_out, not_342_out, not_343_out, not_344_out, not_345_out, not_346_out,
       not_347_out, not_348_out, not_349_out, not_350_out, not_351_out, not_352_out, not_353_out,
       not_354_out, not_355_out, not_356_out, not_357_out, not_358_out, not_359_out, not_360_out,
       not_361_out, not_362_out, not_363_out, not_364_out, not_365_out, not_366_out, not_367_out,
       not_368_out, not_369_out, not_370_out, not_371_out, not_372_out, not_373_out, not_374_out,
       not_375_out, not_376_out, not_377_out, not_378_out, not_379_out, not_380_out, not_381_out,
       not_382_out, not_383_out, not_384_out, not_385_out, not_386_out, not_387_out, not_388_out,
       not_389_out, not_390_out, not_391_out, not_392_out, not_393_out, not_394_out, not_395_out,
       not_396_out, not_397_out, not_398_out, not_399_out, not_400_out, not_401_out, not_402_out,
       not_403_out, not_404_out, not_405_out, not_406_out, not_407_out, not_408_out, not_409_out,
       not_410_out, not_411_out, not_412_out, not_413_out, not_414_out, not_415_out, not_416_out,
       not_417_out, not_418_out, not_419_out, not_420_out, not_421_out, not_422_out, not_423_out,
       not_424_out, not_425_out, not_426_out, not_427_out, not_428_out, not_429_out, not_430_out,
       not_431_out, not_432_out, not_433_out, not_434_out, not_435_out, not_436_out, not_437_out,
       not_438_out, not_439_out, not_440_out, not_441_out, not_442_out, not_443_out, not_444_out,
       not_445_out, not_446_out, not_447_out, not_448_out, not_449_out, not_450_out, not_451_out,
       not_452_out, not_453_out, not_454_out, not_455_out, not_456_out, not_457_out, not_458_out,
       not_459_out, not_460_out, not_461_out, not_462_out, not_463_out, not_464_out, not_465_out,
       not_466_out, not_467_out, not_468_out, not_469_out, not_470_out, not_471_out, not_472_out,
       not_473_out, not_474_out, not_475_out, not_476_out, not_477_out, not_478_out, not_479_out,
       not_480_out, not_481_out, not_482_out, not_483_out, not_484_out, not_485_out, not_486_out,
       not_487_out, not_488_out, not_489_out, not_490_out, not_491_out, not_492_out, not_493_out,
       not_494_out, not_495_out, not_496_out, not_497_out, not_498_out, not_499_out, not_500_out,
       not_501_out, not_502_out, not_503_out, not_504_out, not_505_out, not_506_out, not_507_out,
       not_508_out, not_509_out, not_510_out, not_511_out, not_512_out, not_513_out, not_514_out,
       not_515_out, not_516_out, not_517_out, not_518_out, not_519_out, not_520_out, not_521_out,
       not_522_out, not_523_out, not_524_out, not_525_out, not_526_out, not_527_out, not_528_out,
       not_529_out, not_530_out, not_531_out, not_532_out, not_533_out, not_534_out, not_535_out,
       not_536_out, not_537_out, not_538_out, not_539_out, not_540_out, not_541_out, not_542_out,
       not_543_out, not_544_out, not_545_out, not_546_out, not_547_out, not_548_out, not_549_out,
       not_550_out, not_551_out, not_552_out, not_553_out, not_554_out, not_555_out, not_556_out,
       not_557_out, not_558_out, not_559_out, not_560_out, not_561_out, not_562_out, not_563_out,
       not_564_out, not_565_out, not_566_out, not_567_out, not_568_out, not_569_out, not_570_out,
       not_571_out, not_572_out, not_573_out, not_574_out, not_575_out, not_576_out, not_577_out,
       not_578_out, not_579_out, not_580_out, not_581_out, not_582_out, not_583_out, not_584_out,
       not_585_out, not_586_out, not_587_out, not_588_out, not_589_out, not_590_out, not_591_out,
       not_592_out, not_593_out, not_594_out, not_595_out, not_596_out, not_597_out, not_598_out,
       not_599_out, not_600_out, not_601_out, not_602_out, not_603_out, not_604_out, not_605_out,
       not_606_out, not_607_out, not_608_out, not_609_out, not_610_out, not_611_out, not_612_out,
       not_613_out, not_614_out, not_615_out, not_616_out, not_617_out, not_618_out, not_619_out,
       not_620_out, not_621_out, not_622_out, not_623_out, not_624_out, not_625_out, not_626_out,
       not_627_out, not_628_out, not_629_out, not_630_out, not_631_out, not_632_out, not_633_out,
       not_634_out, not_635_out, not_636_out, not_637_out, not_638_out, not_639_out, not_640_out,
       not_641_out, not_642_out, not_643_out, not_644_out, not_645_out, not_646_out, not_647_out,
       not_648_out, not_649_out, not_650_out, not_651_out, not_652_out, not_653_out, not_654_out,
       not_655_out, not_656_out, not_657_out, not_658_out, not_659_out, not_660_out, not_661_out,
       not_662_out, not_663_out, not_664_out, not_665_out, not_666_out, not_667_out, not_668_out,
       not_669_out, not_670_out, not_671_out, not_672_out, not_673_out, not_674_out, not_675_out,
       not_676_out, not_677_out, not_678_out, not_679_out, not_680_out, not_681_out, not_682_out,
       not_683_out, not_684_out, not_685_out, not_686_out, not_687_out, not_688_out, not_689_out,
       not_690_out, not_691_out, not_692_out, not_693_out, not_694_out, not_695_out, not_696_out,
       not_697_out, not_698_out, not_699_out, not_700_out, not_701_out, not_702_out, not_703_out,
       not_704_out, not_705_out, not_706_out, not_707_out, not_708_out, not_709_out, not_710_out,
       not_711_out, not_712_out, not_713_out, not_714_out, not_715_out, not_716_out, not_717_out,
       not_718_out, not_719_out, not_720_out, not_721_out, not_722_out, not_723_out, not_724_out,
       not_725_out, not_726_out, not_727_out, not_728_out, not_729_out, not_730_out, not_731_out,
       not_732_out, not_733_out, not_734_out, not_735_out, not_736_out, not_737_out, not_738_out,
       not_739_out, not_740_out, not_741_out, not_742_out, not_743_out, not_744_out, not_745_out,
       not_746_out, not_747_out, not_748_out, not_749_out, not_750_out, not_751_out, not_752_out,
       not_753_out, not_754_out, not_755_out, not_756_out, not_757_out, not_758_out, not_759_out,
       not_760_out, not_761_out, not_762_out, not_763_out, not_764_out, not_765_out, not_766_out,
       not_767_out, not_768_out, not_769_out, not_770_out, not_771_out, not_772_out, not_773_out,
       not_774_out, not_775_out, not_776_out, not_777_out, not_778_out, not_779_out, not_780_out,
       not_781_out, not_782_out, not_783_out, not_784_out, not_785_out, not_786_out, not_787_out,
       not_788_out, not_789_out, not_790_out, not_791_out, not_792_out, not_793_out, not_794_out,
       not_795_out, not_796_out, not_797_out, not_798_out, not_799_out, not_800_out, not_801_out,
       not_802_out, not_803_out, not_804_out, not_805_out, not_806_out, not_807_out, not_808_out,
       not_809_out, not_810_out, not_811_out, not_812_out, not_813_out, not_814_out, not_815_out,
       not_816_out, not_817_out, not_818_out, not_819_out, not_820_out, not_821_out, not_822_out,
       not_823_out, not_824_out, not_825_out, not_826_out, not_827_out, not_828_out, not_829_out,
       not_830_out, not_831_out, not_832_out, not_833_out, not_834_out, not_835_out, not_836_out,
       not_837_out, not_838_out, not_839_out, not_840_out, not_841_out, not_842_out, not_843_out,
       not_844_out, not_845_out, not_846_out, not_847_out, not_848_out, not_849_out, not_850_out,
       not_851_out, not_852_out, not_853_out, not_854_out, not_855_out, not_856_out, not_857_out,
       not_858_out, not_859_out, not_860_out, not_861_out, not_862_out, not_863_out, not_864_out,
       not_865_out, not_866_out, not_867_out, not_868_out, not_869_out, not_870_out, not_871_out,
       not_872_out, not_873_out, not_874_out, not_875_out, not_876_out, not_877_out, not_878_out,
       not_879_out, not_880_out, not_881_out, not_882_out, not_883_out, not_884_out, not_885_out,
       not_886_out, not_887_out, not_888_out, not_889_out, not_890_out, not_891_out, not_892_out,
       not_893_out, not_894_out, not_895_out, not_896_out, not_897_out, not_898_out, not_899_out,
       not_900_out, not_901_out, not_902_out, not_903_out, not_904_out, not_905_out, not_906_out,
       not_907_out, not_908_out, not_909_out, not_910_out, not_911_out, not_912_out, not_913_out,
       not_914_out, not_915_out, not_916_out, not_917_out, not_918_out, not_919_out, not_920_out,
       not_921_out, not_922_out, not_923_out, not_924_out, not_925_out, not_926_out, not_927_out,
       not_928_out, not_929_out, not_930_out, not_931_out, not_932_out, not_933_out, not_934_out,
       not_935_out, not_936_out, not_937_out, not_938_out, not_939_out, not_940_out, not_941_out,
       not_942_out, not_943_out, not_944_out, not_945_out, not_946_out, not_947_out, not_948_out,
       not_949_out, not_950_out, not_951_out, not_952_out, not_953_out, not_954_out, not_955_out,
       not_956_out, not_957_out, not_958_out, not_959_out, not_960_out, not_961_out, not_962_out,
       not_963_out, not_964_out, not_965_out, not_966_out, not_967_out, not_968_out, not_969_out,
       not_970_out, not_971_out, not_972_out, not_973_out, not_974_out, not_975_out, not_976_out,
       not_977_out, not_978_out, not_979_out, not_980_out, not_981_out, not_982_out, not_983_out,
       not_984_out, not_985_out, not_986_out, not_987_out, not_988_out, not_989_out, not_990_out,
       not_991_out, not_992_out, not_993_out, not_994_out, not_995_out, not_996_out, not_997_out,
       not_998_out, not_999_out, not_1000_out, not_1001_out, not_1002_out, not_1003_out, not_1004_out,
       not_1005_out, not_1006_out, not_1007_out, not_1008_out, not_1009_out, not_1010_out, not_1011_out,
       not_1012_out, not_1013_out, not_1014_out, not_1015_out, not_1016_out, not_1017_out, not_1018_out,
       not_1019_out, not_1020_out, not_1021_out, not_1022_out, not_1023_out, not_1024_out, not_1025_out,
       not_1026_out, not_1027_out, not_1028_out, not_1029_out, not_1030_out, not_1031_out, not_1032_out,
       not_1033_out, not_1034_out, not_1035_out, not_1036_out, not_1037_out, not_1038_out, not_1039_out,
       not_1040_out, not_1041_out, not_1042_out, not_1043_out, not_1044_out, not_1045_out, not_1046_out,
       not_1047_out, not_1048_out, not_1049_out, not_1050_out, not_1051_out, not_1052_out, not_1053_out,
       not_1054_out, not_1055_out, not_1056_out, not_1057_out, not_1058_out, not_1059_out, not_1060_out,
       not_1061_out, not_1062_out, not_1063_out, not_1064_out, not_1065_out, not_1066_out, not_1067_out,
       not_1068_out, not_1069_out, not_1070_out, not_1071_out, not_1072_out, not_1073_out, not_1074_out,
       not_1075_out, not_1076_out, not_1077_out, not_1078_out, not_1079_out, not_1080_out, not_1081_out,
       not_1082_out, not_1083_out, not_1084_out, not_1085_out, not_1086_out, not_1087_out, not_1088_out,
       not_1089_out, not_1090_out, not_1091_out, not_1092_out, not_1093_out, not_1094_out, not_1095_out,
       not_1096_out, not_1097_out, not_1098_out, not_1099_out, not_1100_out, not_1101_out, not_1102_out,
       not_1103_out, not_1104_out, not_1105_out, not_1106_out, not_1107_out, not_1108_out, not_1109_out,
       not_1110_out, not_1111_out, not_1112_out, not_1113_out, not_1114_out, not_1115_out, not_1116_out,
       not_1117_out, not_1118_out, not_1119_out, not_1120_out, not_1121_out, not_1122_out, not_1123_out,
       not_1124_out, not_1125_out, not_1126_out, not_1127_out, not_1128_out, not_1129_out, not_1130_out,
       not_1131_out, not_1132_out, not_1133_out, not_1134_out, not_1135_out, not_1136_out, not_1137_out,
       not_1138_out, not_1139_out, not_1140_out, not_1141_out, not_1142_out, not_1143_out, not_1144_out,
       not_1145_out, not_1146_out, not_1147_out, not_1148_out, not_1149_out, not_1150_out, not_1151_out,
       not_1152_out, or_1_out, or_2_out, or_3_out, or_4_out, or_5_out, or_6_out, or_7_out, or_8_out,
       or_9_out, or_10_out, or_11_out, or_13_out, or_14_out;

  not not_1 (not_1_out, B);
  not not_2 (not_2_out, C);
  not not_3 (not_3_out, D);
  not not_4 (not_4_out, F);
  not not_5 (not_5_out, H);
  not not_6 (not_6_out, A);
  not not_7 (not_7_out, B);
  not not_8 (not_8_out, C);
  not not_9 (not_9_out, E);
  not not_10 (not_10_out, A);
  not not_11 (not_11_out, B);
  not not_12 (not_12_out, C);
  not not_13 (not_13_out, F);
  not not_14 (not_14_out, H);
  not not_15 (not_15_out, A);
  not not_16 (not_16_out, C);
  not not_17 (not_17_out, E);
  not not_18 (not_18_out, F);
  not not_19 (not_19_out, A);
  not not_20 (not_20_out, C);
  not not_21 (not_21_out, E);
  not not_22 (not_22_out, H);
  not not_23 (not_23_out, B);
  not not_24 (not_24_out, C);
  not not_25 (not_25_out, E);
  not not_26 (not_26_out, F);
  not not_27 (not_27_out, H);
  not not_28 (not_28_out, B);
  not not_29 (not_29_out, D);
  not not_30 (not_30_out, E);
  not not_31 (not_31_out, B);
  not not_32 (not_32_out, D);
  not not_33 (not_33_out, A);
  not not_34 (not_34_out, C);
  not not_35 (not_35_out, D);
  not not_36 (not_36_out, G);
  not not_37 (not_37_out, A);
  not not_38 (not_38_out, C);
  not not_39 (not_39_out, G);
  not not_40 (not_40_out, A);
  not not_41 (not_41_out, D);
  not not_42 (not_42_out, G);
  not not_43 (not_43_out, A);
  not not_44 (not_44_out, B);
  not not_45 (not_45_out, E);
  not not_46 (not_46_out, F);
  not not_47 (not_47_out, H);
  not not_48 (not_48_out, B);
  not not_49 (not_49_out, C);
  not not_50 (not_50_out, F);
  not not_51 (not_51_out, B);
  not not_52 (not_52_out, F);
  not not_53 (not_53_out, G);
  not not_54 (not_54_out, B);
  not not_55 (not_55_out, C);
  not not_56 (not_56_out, H);
  not not_57 (not_57_out, B);
  not not_58 (not_58_out, G);
  not not_59 (not_59_out, H);
  not not_60 (not_60_out, A);
  not not_61 (not_61_out, B);
  not not_62 (not_62_out, E);
  not not_63 (not_63_out, G);
  not not_64 (not_64_out, A);
  not not_65 (not_65_out, B);
  not not_66 (not_66_out, F);
  not not_67 (not_67_out, G);
  not not_68 (not_68_out, H);
  not not_69 (not_69_out, A);
  not not_70 (not_70_out, E);
  not not_71 (not_71_out, F);
  not not_72 (not_72_out, G);
  not not_73 (not_73_out, B);
  not not_74 (not_74_out, E);
  not not_75 (not_75_out, F);
  not not_76 (not_76_out, G);
  not not_77 (not_77_out, H);
  not not_78 (not_78_out, A);
  not not_79 (not_79_out, B);
  not not_80 (not_80_out, D);
  not not_81 (not_81_out, E);
  not not_82 (not_82_out, A);
  not not_83 (not_83_out, B);
  not not_84 (not_84_out, D);
  not not_85 (not_85_out, E);
  not not_86 (not_86_out, A);
  not not_87 (not_87_out, B);
  not not_88 (not_88_out, E);
  not not_89 (not_89_out, A);
  not not_90 (not_90_out, B);
  not not_91 (not_91_out, A);
  not not_92 (not_92_out, F);
  not not_93 (not_93_out, A);
  not not_94 (not_94_out, H);
  not not_95 (not_95_out, A);
  not not_96 (not_96_out, D);
  not not_97 (not_97_out, F);
  not not_98 (not_98_out, D);
  not not_99 (not_99_out, E);
  not not_100 (not_100_out, F);
  not not_101 (not_101_out, A);
  not not_102 (not_102_out, D);
  not not_103 (not_103_out, H);
  not not_104 (not_104_out, C);
  not not_105 (not_105_out, D);
  not not_106 (not_106_out, G);
  not not_107 (not_107_out, A);
  not not_108 (not_108_out, C);
  not not_109 (not_109_out, D);
  not not_110 (not_110_out, C);
  not not_111 (not_111_out, F);
  not not_112 (not_112_out, H);
  not not_113 (not_113_out, F);
  not not_114 (not_114_out, G);
  not not_115 (not_115_out, H);
  not not_116 (not_116_out, A);
  not not_117 (not_117_out, E);
  not not_118 (not_118_out, C);
  not not_119 (not_119_out, F);
  not not_120 (not_120_out, G);
  not not_121 (not_121_out, A);
  not not_122 (not_122_out, E);
  not not_123 (not_123_out, F);
  not not_124 (not_124_out, D);
  not not_125 (not_125_out, F);
  not not_126 (not_126_out, A);
  not not_127 (not_127_out, D);
  not not_128 (not_128_out, E);
  not not_129 (not_129_out, A);
  not not_130 (not_130_out, E);
  not not_131 (not_131_out, H);
  not not_132 (not_132_out, D);
  not not_133 (not_133_out, H);
  not not_134 (not_134_out, B);
  not not_135 (not_135_out, C);
  not not_136 (not_136_out, D);
  not not_137 (not_137_out, G);
  not not_138 (not_138_out, H);
  not not_139 (not_139_out, B);
  not not_140 (not_140_out, D);
  not not_141 (not_141_out, F);
  not not_142 (not_142_out, H);
  not not_143 (not_143_out, C);
  not not_144 (not_144_out, D);
  not not_145 (not_145_out, E);
  not not_146 (not_146_out, G);
  not not_147 (not_147_out, C);
  not not_148 (not_148_out, D);
  not not_149 (not_149_out, F);
  not not_150 (not_150_out, G);
  not not_151 (not_151_out, H);
  not not_152 (not_152_out, B);
  not not_153 (not_153_out, C);
  not not_154 (not_154_out, F);
  not not_155 (not_155_out, G);
  not not_156 (not_156_out, C);
  not not_157 (not_157_out, D);
  not not_158 (not_158_out, C);
  not not_159 (not_159_out, B);
  not not_160 (not_160_out, F);
  not not_161 (not_161_out, B);
  not not_162 (not_162_out, C);
  not not_163 (not_163_out, G);
  not not_164 (not_164_out, B);
  not not_165 (not_165_out, H);
  not not_166 (not_166_out, B);
  not not_167 (not_167_out, E);
  not not_168 (not_168_out, E);
  not not_169 (not_169_out, F);
  not not_170 (not_170_out, D);
  not not_171 (not_171_out, G);
  not not_172 (not_172_out, G);
  not not_173 (not_173_out, E);
  not not_174 (not_174_out, F);
  not not_175 (not_175_out, H);
  not not_176 (not_176_out, C);
  not not_177 (not_177_out, E);
  not not_178 (not_178_out, G);
  not not_179 (not_179_out, C);
  not not_180 (not_180_out, D);
  not not_181 (not_181_out, E);
  not not_182 (not_182_out, D);
  not not_183 (not_183_out, E);
  not not_184 (not_184_out, G);
  not not_185 (not_185_out, C);
  not not_186 (not_186_out, C);
  not not_187 (not_187_out, G);
  not not_188 (not_188_out, H);
  not not_189 (not_189_out, G);
  not not_190 (not_190_out, A);
  not not_191 (not_191_out, B);
  not not_192 (not_192_out, C);
  not not_193 (not_193_out, E);
  not not_194 (not_194_out, F);
  not not_195 (not_195_out, A);
  not not_196 (not_196_out, B);
  not not_197 (not_197_out, C);
  not not_198 (not_198_out, D);
  not not_199 (not_199_out, G);
  not not_200 (not_200_out, A);
  not not_201 (not_201_out, B);
  not not_202 (not_202_out, D);
  not not_203 (not_203_out, H);
  not not_204 (not_204_out, B);
  not not_205 (not_205_out, D);
  not not_206 (not_206_out, E);
  not not_207 (not_207_out, H);
  not not_208 (not_208_out, A);
  not not_209 (not_209_out, B);
  not not_210 (not_210_out, C);
  not not_211 (not_211_out, G);
  not not_212 (not_212_out, A);
  not not_213 (not_213_out, C);
  not not_214 (not_214_out, F);
  not not_215 (not_215_out, G);
  not not_216 (not_216_out, A);
  not not_217 (not_217_out, B);
  not not_218 (not_218_out, C);
  not not_219 (not_219_out, D);
  not not_220 (not_220_out, A);
  not not_221 (not_221_out, B);
  not not_222 (not_222_out, D);
  not not_223 (not_223_out, G);
  not not_224 (not_224_out, B);
  not not_225 (not_225_out, C);
  not not_226 (not_226_out, F);
  not not_227 (not_227_out, H);
  not not_228 (not_228_out, B);
  not not_229 (not_229_out, F);
  not not_230 (not_230_out, G);
  not not_231 (not_231_out, H);
  not not_232 (not_232_out, A);
  not not_233 (not_233_out, B);
  not not_234 (not_234_out, C);
  not not_235 (not_235_out, E);
  not not_236 (not_236_out, A);
  not not_237 (not_237_out, C);
  not not_238 (not_238_out, E);
  not not_239 (not_239_out, F);
  not not_240 (not_240_out, A);
  not not_241 (not_241_out, B);
  not not_242 (not_242_out, E);
  not not_243 (not_243_out, F);
  not not_244 (not_244_out, G);
  not not_245 (not_245_out, A);
  not not_246 (not_246_out, D);
  not not_247 (not_247_out, E);
  not not_248 (not_248_out, A);
  not not_249 (not_249_out, B);
  not not_250 (not_250_out, F);
  not not_251 (not_251_out, A);
  not not_252 (not_252_out, B);
  not not_253 (not_253_out, E);
  not not_254 (not_254_out, A);
  not not_255 (not_255_out, B);
  not not_256 (not_256_out, A);
  not not_257 (not_257_out, C);
  not not_258 (not_258_out, D);
  not not_259 (not_259_out, E);
  not not_260 (not_260_out, G);
  not not_261 (not_261_out, A);
  not not_262 (not_262_out, D);
  not not_263 (not_263_out, F);
  not not_264 (not_264_out, H);
  not not_265 (not_265_out, C);
  not not_266 (not_266_out, D);
  not not_267 (not_267_out, G);
  not not_268 (not_268_out, H);
  not not_269 (not_269_out, A);
  not not_270 (not_270_out, C);
  not not_271 (not_271_out, D);
  not not_272 (not_272_out, A);
  not not_273 (not_273_out, C);
  not not_274 (not_274_out, G);
  not not_275 (not_275_out, A);
  not not_276 (not_276_out, H);
  not not_277 (not_277_out, E);
  not not_278 (not_278_out, H);
  not not_279 (not_279_out, A);
  not not_280 (not_280_out, C);
  not not_281 (not_281_out, D);
  not not_282 (not_282_out, F);
  not not_283 (not_283_out, H);
  not not_284 (not_284_out, A);
  not not_285 (not_285_out, E);
  not not_286 (not_286_out, A);
  not not_287 (not_287_out, D);
  not not_288 (not_288_out, G);
  not not_289 (not_289_out, A);
  not not_290 (not_290_out, G);
  not not_291 (not_291_out, A);
  not not_292 (not_292_out, E);
  not not_293 (not_293_out, F);
  not not_294 (not_294_out, A);
  not not_295 (not_295_out, F);
  not not_296 (not_296_out, B);
  not not_297 (not_297_out, C);
  not not_298 (not_298_out, E);
  not not_299 (not_299_out, G);
  not not_300 (not_300_out, B);
  not not_301 (not_301_out, C);
  not not_302 (not_302_out, F);
  not not_303 (not_303_out, G);
  not not_304 (not_304_out, H);
  not not_305 (not_305_out, C);
  not not_306 (not_306_out, E);
  not not_307 (not_307_out, F);
  not not_308 (not_308_out, G);
  not not_309 (not_309_out, B);
  not not_310 (not_310_out, C);
  not not_311 (not_311_out, D);
  not not_312 (not_312_out, E);
  not not_313 (not_313_out, B);
  not not_314 (not_314_out, C);
  not not_315 (not_315_out, C);
  not not_316 (not_316_out, F);
  not not_317 (not_317_out, B);
  not not_318 (not_318_out, C);
  not not_319 (not_319_out, F);
  not not_320 (not_320_out, G);
  not not_321 (not_321_out, B);
  not not_322 (not_322_out, C);
  not not_323 (not_323_out, G);
  not not_324 (not_324_out, H);
  not not_325 (not_325_out, B);
  not not_326 (not_326_out, F);
  not not_327 (not_327_out, H);
  not not_328 (not_328_out, C);
  not not_329 (not_329_out, F);
  not not_330 (not_330_out, G);
  not not_331 (not_331_out, H);
  not not_332 (not_332_out, B);
  not not_333 (not_333_out, E);
  not not_334 (not_334_out, F);
  not not_335 (not_335_out, D);
  not not_336 (not_336_out, E);
  not not_337 (not_337_out, G);
  not not_338 (not_338_out, B);
  not not_339 (not_339_out, G);
  not not_340 (not_340_out, D);
  not not_341 (not_341_out, B);
  not not_342 (not_342_out, E);
  not not_343 (not_343_out, E);
  not not_344 (not_344_out, F);
  not not_345 (not_345_out, G);
  not not_346 (not_346_out, C);
  not not_347 (not_347_out, D);
  not not_348 (not_348_out, E);
  not not_349 (not_349_out, C);
  not not_350 (not_350_out, D);
  not not_351 (not_351_out, G);
  not not_352 (not_352_out, D);
  not not_353 (not_353_out, H);
  not not_354 (not_354_out, C);
  not not_355 (not_355_out, E);
  not not_356 (not_356_out, D);
  not not_357 (not_357_out, F);
  not not_358 (not_358_out, G);
  not not_359 (not_359_out, E);
  not not_360 (not_360_out, G);
  not not_361 (not_361_out, D);
  not not_362 (not_362_out, F);
  not not_363 (not_363_out, B);
  not not_364 (not_364_out, C);
  not not_365 (not_365_out, D);
  not not_366 (not_366_out, F);
  not not_367 (not_367_out, H);
  not not_368 (not_368_out, A);
  not not_369 (not_369_out, B);
  not not_370 (not_370_out, C);
  not not_371 (not_371_out, E);
  not not_372 (not_372_out, F);
  not not_373 (not_373_out, A);
  not not_374 (not_374_out, B);
  not not_375 (not_375_out, C);
  not not_376 (not_376_out, F);
  not not_377 (not_377_out, H);
  not not_378 (not_378_out, A);
  not not_379 (not_379_out, C);
  not not_380 (not_380_out, E);
  not not_381 (not_381_out, H);
  not not_382 (not_382_out, B);
  not not_383 (not_383_out, C);
  not not_384 (not_384_out, E);
  not not_385 (not_385_out, F);
  not not_386 (not_386_out, H);
  not not_387 (not_387_out, A);
  not not_388 (not_388_out, B);
  not not_389 (not_389_out, C);
  not not_390 (not_390_out, D);
  not not_391 (not_391_out, G);
  not not_392 (not_392_out, A);
  not not_393 (not_393_out, B);
  not not_394 (not_394_out, C);
  not not_395 (not_395_out, D);
  not not_396 (not_396_out, G);
  not not_397 (not_397_out, A);
  not not_398 (not_398_out, B);
  not not_399 (not_399_out, C);
  not not_400 (not_400_out, D);
  not not_401 (not_401_out, A);
  not not_402 (not_402_out, B);
  not not_403 (not_403_out, D);
  not not_404 (not_404_out, G);
  not not_405 (not_405_out, A);
  not not_406 (not_406_out, B);
  not not_407 (not_407_out, E);
  not not_408 (not_408_out, F);
  not not_409 (not_409_out, H);
  not not_410 (not_410_out, A);
  not not_411 (not_411_out, B);
  not not_412 (not_412_out, C);
  not not_413 (not_413_out, E);
  not not_414 (not_414_out, A);
  not not_415 (not_415_out, C);
  not not_416 (not_416_out, E);
  not not_417 (not_417_out, F);
  not not_418 (not_418_out, B);
  not not_419 (not_419_out, C);
  not not_420 (not_420_out, H);
  not not_421 (not_421_out, B);
  not not_422 (not_422_out, G);
  not not_423 (not_423_out, H);
  not not_424 (not_424_out, B);
  not not_425 (not_425_out, C);
  not not_426 (not_426_out, F);
  not not_427 (not_427_out, G);
  not not_428 (not_428_out, A);
  not not_429 (not_429_out, C);
  not not_430 (not_430_out, G);
  not not_431 (not_431_out, A);
  not not_432 (not_432_out, B);
  not not_433 (not_433_out, E);
  not not_434 (not_434_out, F);
  not not_435 (not_435_out, G);
  not not_436 (not_436_out, A);
  not not_437 (not_437_out, B);
  not not_438 (not_438_out, F);
  not not_439 (not_439_out, G);
  not not_440 (not_440_out, H);
  not not_441 (not_441_out, A);
  not not_442 (not_442_out, E);
  not not_443 (not_443_out, G);
  not not_444 (not_444_out, H);
  not not_445 (not_445_out, B);
  not not_446 (not_446_out, E);
  not not_447 (not_447_out, F);
  not not_448 (not_448_out, G);
  not not_449 (not_449_out, H);
  not not_450 (not_450_out, A);
  not not_451 (not_451_out, D);
  not not_452 (not_452_out, E);
  not not_453 (not_453_out, A);
  not not_454 (not_454_out, D);
  not not_455 (not_455_out, E);
  not not_456 (not_456_out, H);
  not not_457 (not_457_out, A);
  not not_458 (not_458_out, B);
  not not_459 (not_459_out, F);
  not not_460 (not_460_out, A);
  not not_461 (not_461_out, H);
  not not_462 (not_462_out, A);
  not not_463 (not_463_out, B);
  not not_464 (not_464_out, E);
  not not_465 (not_465_out, A);
  not not_466 (not_466_out, B);
  not not_467 (not_467_out, A);
  not not_468 (not_468_out, F);
  not not_469 (not_469_out, A);
  not not_470 (not_470_out, C);
  not not_471 (not_471_out, D);
  not not_472 (not_472_out, E);
  not not_473 (not_473_out, G);
  not not_474 (not_474_out, A);
  not not_475 (not_475_out, D);
  not not_476 (not_476_out, H);
  not not_477 (not_477_out, D);
  not not_478 (not_478_out, E);
  not not_479 (not_479_out, H);
  not not_480 (not_480_out, A);
  not not_481 (not_481_out, C);
  not not_482 (not_482_out, E);
  not not_483 (not_483_out, G);
  not not_484 (not_484_out, A);
  not not_485 (not_485_out, C);
  not not_486 (not_486_out, F);
  not not_487 (not_487_out, G);
  not not_488 (not_488_out, A);
  not not_489 (not_489_out, C);
  not not_490 (not_490_out, D);
  not not_491 (not_491_out, C);
  not not_492 (not_492_out, F);
  not not_493 (not_493_out, H);
  not not_494 (not_494_out, F);
  not not_495 (not_495_out, G);
  not not_496 (not_496_out, H);
  not not_497 (not_497_out, A);
  not not_498 (not_498_out, C);
  not not_499 (not_499_out, A);
  not not_500 (not_500_out, D);
  not not_501 (not_501_out, E);
  not not_502 (not_502_out, H);
  not not_503 (not_503_out, A);
  not not_504 (not_504_out, E);
  not not_505 (not_505_out, A);
  not not_506 (not_506_out, D);
  not not_507 (not_507_out, G);
  not not_508 (not_508_out, A);
  not not_509 (not_509_out, G);
  not not_510 (not_510_out, A);
  not not_511 (not_511_out, E);
  not not_512 (not_512_out, F);
  not not_513 (not_513_out, B);
  not not_514 (not_514_out, C);
  not not_515 (not_515_out, D);
  not not_516 (not_516_out, G);
  not not_517 (not_517_out, H);
  not not_518 (not_518_out, B);
  not not_519 (not_519_out, D);
  not not_520 (not_520_out, F);
  not not_521 (not_521_out, H);
  not not_522 (not_522_out, B);
  not not_523 (not_523_out, C);
  not not_524 (not_524_out, E);
  not not_525 (not_525_out, G);
  not not_526 (not_526_out, B);
  not not_527 (not_527_out, C);
  not not_528 (not_528_out, D);
  not not_529 (not_529_out, E);
  not not_530 (not_530_out, B);
  not not_531 (not_531_out, D);
  not not_532 (not_532_out, E);
  not not_533 (not_533_out, G);
  not not_534 (not_534_out, C);
  not not_535 (not_535_out, F);
  not not_536 (not_536_out, G);
  not not_537 (not_537_out, H);
  not not_538 (not_538_out, C);
  not not_539 (not_539_out, D);
  not not_540 (not_540_out, F);
  not not_541 (not_541_out, C);
  not not_542 (not_542_out, D);
  not not_543 (not_543_out, H);
  not not_544 (not_544_out, B);
  not not_545 (not_545_out, C);
  not not_546 (not_546_out, B);
  not not_547 (not_547_out, H);
  not not_548 (not_548_out, B);
  not not_549 (not_549_out, E);
  not not_550 (not_550_out, F);
  not not_551 (not_551_out, B);
  not not_552 (not_552_out, F);
  not not_553 (not_553_out, H);
  not not_554 (not_554_out, E);
  not not_555 (not_555_out, H);
  not not_556 (not_556_out, D);
  not not_557 (not_557_out, G);
  not not_558 (not_558_out, H);
  not not_559 (not_559_out, B);
  not not_560 (not_560_out, G);
  not not_561 (not_561_out, B);
  not not_562 (not_562_out, D);
  not not_563 (not_563_out, B);
  not not_564 (not_564_out, E);
  not not_565 (not_565_out, E);
  not not_566 (not_566_out, F);
  not not_567 (not_567_out, C);
  not not_568 (not_568_out, E);
  not not_569 (not_569_out, F);
  not not_570 (not_570_out, G);
  not not_571 (not_571_out, C);
  not not_572 (not_572_out, D);
  not not_573 (not_573_out, E);
  not not_574 (not_574_out, C);
  not not_575 (not_575_out, D);
  not not_576 (not_576_out, G);
  not not_577 (not_577_out, C);
  not not_578 (not_578_out, E);
  not not_579 (not_579_out, G);
  not not_580 (not_580_out, C);
  not not_581 (not_581_out, G);
  not not_582 (not_582_out, H);
  not not_583 (not_583_out, F);
  not not_584 (not_584_out, H);
  not not_585 (not_585_out, C);
  not not_586 (not_586_out, E);
  not not_587 (not_587_out, C);
  not not_588 (not_588_out, D);
  not not_589 (not_589_out, E);
  not not_590 (not_590_out, G);
  not not_591 (not_591_out, E);
  not not_592 (not_592_out, G);
  not not_593 (not_593_out, D);
  not not_594 (not_594_out, F);
  not not_595 (not_595_out, D);
  not not_596 (not_596_out, G);
  not not_597 (not_597_out, A);
  not not_598 (not_598_out, C);
  not not_599 (not_599_out, E);
  not not_600 (not_600_out, G);
  not not_601 (not_601_out, H);
  not not_602 (not_602_out, A);
  not not_603 (not_603_out, B);
  not not_604 (not_604_out, D);
  not not_605 (not_605_out, E);
  not not_606 (not_606_out, H);
  not not_607 (not_607_out, A);
  not not_608 (not_608_out, C);
  not not_609 (not_609_out, D);
  not not_610 (not_610_out, E);
  not not_611 (not_611_out, G);
  not not_612 (not_612_out, A);
  not not_613 (not_613_out, B);
  not not_614 (not_614_out, C);
  not not_615 (not_615_out, F);
  not not_616 (not_616_out, G);
  not not_617 (not_617_out, A);
  not not_618 (not_618_out, C);
  not not_619 (not_619_out, H);
  not not_620 (not_620_out, A);
  not not_621 (not_621_out, C);
  not not_622 (not_622_out, D);
  not not_623 (not_623_out, A);
  not not_624 (not_624_out, B);
  not not_625 (not_625_out, F);
  not not_626 (not_626_out, H);
  not not_627 (not_627_out, A);
  not not_628 (not_628_out, B);
  not not_629 (not_629_out, C);
  not not_630 (not_630_out, E);
  not not_631 (not_631_out, F);
  not not_632 (not_632_out, B);
  not not_633 (not_633_out, C);
  not not_634 (not_634_out, G);
  not not_635 (not_635_out, H);
  not not_636 (not_636_out, A);
  not not_637 (not_637_out, B);
  not not_638 (not_638_out, C);
  not not_639 (not_639_out, G);
  not not_640 (not_640_out, A);
  not not_641 (not_641_out, C);
  not not_642 (not_642_out, F);
  not not_643 (not_643_out, G);
  not not_644 (not_644_out, A);
  not not_645 (not_645_out, B);
  not not_646 (not_646_out, D);
  not not_647 (not_647_out, E);
  not not_648 (not_648_out, B);
  not not_649 (not_649_out, D);
  not not_650 (not_650_out, H);
  not not_651 (not_651_out, A);
  not not_652 (not_652_out, G);
  not not_653 (not_653_out, H);
  not not_654 (not_654_out, A);
  not not_655 (not_655_out, D);
  not not_656 (not_656_out, G);
  not not_657 (not_657_out, A);
  not not_658 (not_658_out, B);
  not not_659 (not_659_out, E);
  not not_660 (not_660_out, F);
  not not_661 (not_661_out, G);
  not not_662 (not_662_out, A);
  not not_663 (not_663_out, E);
  not not_664 (not_664_out, A);
  not not_665 (not_665_out, B);
  not not_666 (not_666_out, F);
  not not_667 (not_667_out, A);
  not not_668 (not_668_out, C);
  not not_669 (not_669_out, D);
  not not_670 (not_670_out, E);
  not not_671 (not_671_out, G);
  not not_672 (not_672_out, A);
  not not_673 (not_673_out, D);
  not not_674 (not_674_out, E);
  not not_675 (not_675_out, F);
  not not_676 (not_676_out, H);
  not not_677 (not_677_out, A);
  not not_678 (not_678_out, C);
  not not_679 (not_679_out, E);
  not not_680 (not_680_out, G);
  not not_681 (not_681_out, C);
  not not_682 (not_682_out, D);
  not not_683 (not_683_out, H);
  not not_684 (not_684_out, D);
  not not_685 (not_685_out, G);
  not not_686 (not_686_out, H);
  not not_687 (not_687_out, A);
  not not_688 (not_688_out, C);
  not not_689 (not_689_out, D);
  not not_690 (not_690_out, A);
  not not_691 (not_691_out, C);
  not not_692 (not_692_out, A);
  not not_693 (not_693_out, E);
  not not_694 (not_694_out, H);
  not not_695 (not_695_out, A);
  not not_696 (not_696_out, E);
  not not_697 (not_697_out, F);
  not not_698 (not_698_out, A);
  not not_699 (not_699_out, D);
  not not_700 (not_700_out, G);
  not not_701 (not_701_out, A);
  not not_702 (not_702_out, D);
  not not_703 (not_703_out, H);
  not not_704 (not_704_out, A);
  not not_705 (not_705_out, G);
  not not_706 (not_706_out, H);
  not not_707 (not_707_out, B);
  not not_708 (not_708_out, C);
  not not_709 (not_709_out, E);
  not not_710 (not_710_out, F);
  not not_711 (not_711_out, G);
  not not_712 (not_712_out, C);
  not not_713 (not_713_out, E);
  not not_714 (not_714_out, H);
  not not_715 (not_715_out, C);
  not not_716 (not_716_out, D);
  not not_717 (not_717_out, E);
  not not_718 (not_718_out, C);
  not not_719 (not_719_out, D);
  not not_720 (not_720_out, G);
  not not_721 (not_721_out, H);
  not not_722 (not_722_out, B);
  not not_723 (not_723_out, C);
  not not_724 (not_724_out, F);
  not not_725 (not_725_out, B);
  not not_726 (not_726_out, C);
  not not_727 (not_727_out, E);
  not not_728 (not_728_out, G);
  not not_729 (not_729_out, C);
  not not_730 (not_730_out, E);
  not not_731 (not_731_out, F);
  not not_732 (not_732_out, G);
  not not_733 (not_733_out, B);
  not not_734 (not_734_out, C);
  not not_735 (not_735_out, C);
  not not_736 (not_736_out, F);
  not not_737 (not_737_out, E);
  not not_738 (not_738_out, G);
  not not_739 (not_739_out, H);
  not not_740 (not_740_out, D);
  not not_741 (not_741_out, E);
  not not_742 (not_742_out, G);
  not not_743 (not_743_out, B);
  not not_744 (not_744_out, F);
  not not_745 (not_745_out, G);
  not not_746 (not_746_out, H);
  not not_747 (not_747_out, D);
  not not_748 (not_748_out, B);
  not not_749 (not_749_out, E);
  not not_750 (not_750_out, F);
  not not_751 (not_751_out, B);
  not not_752 (not_752_out, G);
  not not_753 (not_753_out, F);
  not not_754 (not_754_out, G);
  not not_755 (not_755_out, C);
  not not_756 (not_756_out, D);
  not not_757 (not_757_out, E);
  not not_758 (not_758_out, C);
  not not_759 (not_759_out, E);
  not not_760 (not_760_out, C);
  not not_761 (not_761_out, G);
  not not_762 (not_762_out, H);
  not not_763 (not_763_out, C);
  not not_764 (not_764_out, D);
  not not_765 (not_765_out, G);
  not not_766 (not_766_out, D);
  not not_767 (not_767_out, E);
  not not_768 (not_768_out, G);
  not not_769 (not_769_out, D);
  not not_770 (not_770_out, E);
  not not_771 (not_771_out, H);
  not not_772 (not_772_out, E);
  not not_773 (not_773_out, G);
  not not_774 (not_774_out, D);
  not not_775 (not_775_out, B);
  not not_776 (not_776_out, C);
  not not_777 (not_777_out, D);
  not not_778 (not_778_out, F);
  not not_779 (not_779_out, H);
  not not_780 (not_780_out, A);
  not not_781 (not_781_out, B);
  not not_782 (not_782_out, C);
  not not_783 (not_783_out, F);
  not not_784 (not_784_out, H);
  not not_785 (not_785_out, A);
  not not_786 (not_786_out, C);
  not not_787 (not_787_out, E);
  not not_788 (not_788_out, H);
  not not_789 (not_789_out, B);
  not not_790 (not_790_out, C);
  not not_791 (not_791_out, E);
  not not_792 (not_792_out, F);
  not not_793 (not_793_out, H);
  not not_794 (not_794_out, A);
  not not_795 (not_795_out, C);
  not not_796 (not_796_out, D);
  not not_797 (not_797_out, G);
  not not_798 (not_798_out, H);
  not not_799 (not_799_out, A);
  not not_800 (not_800_out, B);
  not not_801 (not_801_out, E);
  not not_802 (not_802_out, F);
  not not_803 (not_803_out, H);
  not not_804 (not_804_out, B);
  not not_805 (not_805_out, C);
  not not_806 (not_806_out, H);
  not not_807 (not_807_out, B);
  not not_808 (not_808_out, G);
  not not_809 (not_809_out, H);
  not not_810 (not_810_out, A);
  not not_811 (not_811_out, B);
  not not_812 (not_812_out, F);
  not not_813 (not_813_out, G);
  not not_814 (not_814_out, H);
  not not_815 (not_815_out, A);
  not not_816 (not_816_out, E);
  not not_817 (not_817_out, G);
  not not_818 (not_818_out, H);
  not not_819 (not_819_out, B);
  not not_820 (not_820_out, E);
  not not_821 (not_821_out, F);
  not not_822 (not_822_out, G);
  not not_823 (not_823_out, H);
  not not_824 (not_824_out, A);
  not not_825 (not_825_out, D);
  not not_826 (not_826_out, E);
  not not_827 (not_827_out, H);
  not not_828 (not_828_out, A);
  not not_829 (not_829_out, H);
  not not_830 (not_830_out, A);
  not not_831 (not_831_out, D);
  not not_832 (not_832_out, H);
  not not_833 (not_833_out, D);
  not not_834 (not_834_out, E);
  not not_835 (not_835_out, H);
  not not_836 (not_836_out, A);
  not not_837 (not_837_out, C);
  not not_838 (not_838_out, G);
  not not_839 (not_839_out, H);
  not not_840 (not_840_out, C);
  not not_841 (not_841_out, F);
  not not_842 (not_842_out, H);
  not not_843 (not_843_out, F);
  not not_844 (not_844_out, G);
  not not_845 (not_845_out, H);
  not not_846 (not_846_out, A);
  not not_847 (not_847_out, D);
  not not_848 (not_848_out, E);
  not not_849 (not_849_out, H);
  not not_850 (not_850_out, A);
  not not_851 (not_851_out, E);
  not not_852 (not_852_out, H);
  not not_853 (not_853_out, D);
  not not_854 (not_854_out, H);
  not not_855 (not_855_out, B);
  not not_856 (not_856_out, C);
  not not_857 (not_857_out, D);
  not not_858 (not_858_out, G);
  not not_859 (not_859_out, H);
  not not_860 (not_860_out, B);
  not not_861 (not_861_out, D);
  not not_862 (not_862_out, F);
  not not_863 (not_863_out, H);
  not not_864 (not_864_out, C);
  not not_865 (not_865_out, D);
  not not_866 (not_866_out, F);
  not not_867 (not_867_out, G);
  not not_868 (not_868_out, H);
  not not_869 (not_869_out, B);
  not not_870 (not_870_out, C);
  not not_871 (not_871_out, G);
  not not_872 (not_872_out, H);
  not not_873 (not_873_out, C);
  not not_874 (not_874_out, D);
  not not_875 (not_875_out, H);
  not not_876 (not_876_out, B);
  not not_877 (not_877_out, H);
  not not_878 (not_878_out, B);
  not not_879 (not_879_out, F);
  not not_880 (not_880_out, H);
  not not_881 (not_881_out, E);
  not not_882 (not_882_out, H);
  not not_883 (not_883_out, D);
  not not_884 (not_884_out, G);
  not not_885 (not_885_out, H);
  not not_886 (not_886_out, C);
  not not_887 (not_887_out, G);
  not not_888 (not_888_out, H);
  not not_889 (not_889_out, F);
  not not_890 (not_890_out, H);
  not not_891 (not_891_out, C);
  not not_892 (not_892_out, H);
  not not_893 (not_893_out, G);
  not not_894 (not_894_out, H);
  not not_895 (not_895_out, A);
  not not_896 (not_896_out, B);
  not not_897 (not_897_out, C);
  not not_898 (not_898_out, D);
  not not_899 (not_899_out, F);
  not not_900 (not_900_out, A);
  not not_901 (not_901_out, B);
  not not_902 (not_902_out, C);
  not not_903 (not_903_out, E);
  not not_904 (not_904_out, F);
  not not_905 (not_905_out, A);
  not not_906 (not_906_out, B);
  not not_907 (not_907_out, C);
  not not_908 (not_908_out, F);
  not not_909 (not_909_out, A);
  not not_910 (not_910_out, C);
  not not_911 (not_911_out, E);
  not not_912 (not_912_out, B);
  not not_913 (not_913_out, C);
  not not_914 (not_914_out, E);
  not not_915 (not_915_out, F);
  not not_916 (not_916_out, B);
  not not_917 (not_917_out, C);
  not not_918 (not_918_out, D);
  not not_919 (not_919_out, G);
  not not_920 (not_920_out, H);
  not not_921 (not_921_out, A);
  not not_922 (not_922_out, B);
  not not_923 (not_923_out, C);
  not not_924 (not_924_out, G);
  not not_925 (not_925_out, H);
  not not_926 (not_926_out, A);
  not not_927 (not_927_out, C);
  not not_928 (not_928_out, D);
  not not_929 (not_929_out, G);
  not not_930 (not_930_out, A);
  not not_931 (not_931_out, C);
  not not_932 (not_932_out, D);
  not not_933 (not_933_out, H);
  not not_934 (not_934_out, A);
  not not_935 (not_935_out, B);
  not not_936 (not_936_out, E);
  not not_937 (not_937_out, F);
  not not_938 (not_938_out, A);
  not not_939 (not_939_out, B);
  not not_940 (not_940_out, C);
  not not_941 (not_941_out, A);
  not not_942 (not_942_out, B);
  not not_943 (not_943_out, G);
  not not_944 (not_944_out, A);
  not not_945 (not_945_out, B);
  not not_946 (not_946_out, E);
  not not_947 (not_947_out, F);
  not not_948 (not_948_out, G);
  not not_949 (not_949_out, A);
  not not_950 (not_950_out, B);
  not not_951 (not_951_out, F);
  not not_952 (not_952_out, G);
  not not_953 (not_953_out, A);
  not not_954 (not_954_out, E);
  not not_955 (not_955_out, G);
  not not_956 (not_956_out, B);
  not not_957 (not_957_out, E);
  not not_958 (not_958_out, F);
  not not_959 (not_959_out, G);
  not not_960 (not_960_out, A);
  not not_961 (not_961_out, B);
  not not_962 (not_962_out, F);
  not not_963 (not_963_out, H);
  not not_964 (not_964_out, A);
  not not_965 (not_965_out, E);
  not not_966 (not_966_out, H);
  not not_967 (not_967_out, B);
  not not_968 (not_968_out, E);
  not not_969 (not_969_out, F);
  not not_970 (not_970_out, H);
  not not_971 (not_971_out, A);
  not not_972 (not_972_out, D);
  not not_973 (not_973_out, E);
  not not_974 (not_974_out, A);
  not not_975 (not_975_out, D);
  not not_976 (not_976_out, G);
  not not_977 (not_977_out, H);
  not not_978 (not_978_out, B);
  not not_979 (not_979_out, D);
  not not_980 (not_980_out, F);
  not not_981 (not_981_out, A);
  not not_982 (not_982_out, B);
  not not_983 (not_983_out, C);
  not not_984 (not_984_out, D);
  not not_985 (not_985_out, F);
  not not_986 (not_986_out, G);
  not not_987 (not_987_out, H);
  not not_988 (not_988_out, A);
  not not_989 (not_989_out, D);
  not not_990 (not_990_out, E);
  not not_991 (not_991_out, A);
  not not_992 (not_992_out, D);
  not not_993 (not_993_out, D);
  not not_994 (not_994_out, E);
  not not_995 (not_995_out, D);
  not not_996 (not_996_out, A);
  not not_997 (not_997_out, C);
  not not_998 (not_998_out, F);
  not not_999 (not_999_out, A);
  not not_1000 (not_1000_out, F);
  not not_1001 (not_1001_out, G);
  not not_1002 (not_1002_out, C);
  not not_1003 (not_1003_out, G);
  not not_1004 (not_1004_out, H);
  not not_1005 (not_1005_out, A);
  not not_1006 (not_1006_out, C);
  not not_1007 (not_1007_out, G);
  not not_1008 (not_1008_out, A);
  not not_1009 (not_1009_out, C);
  not not_1010 (not_1010_out, H);
  not not_1011 (not_1011_out, A);
  not not_1012 (not_1012_out, D);
  not not_1013 (not_1013_out, E);
  not not_1014 (not_1014_out, A);
  not not_1015 (not_1015_out, E);
  not not_1016 (not_1016_out, D);
  not not_1017 (not_1017_out, A);
  not not_1018 (not_1018_out, G);
  not not_1019 (not_1019_out, H);
  not not_1020 (not_1020_out, F);
  not not_1021 (not_1021_out, B);
  not not_1022 (not_1022_out, D);
  not not_1023 (not_1023_out, E);
  not not_1024 (not_1024_out, F);
  not not_1025 (not_1025_out, C);
  not not_1026 (not_1026_out, D);
  not not_1027 (not_1027_out, E);
  not not_1028 (not_1028_out, H);
  not not_1029 (not_1029_out, C);
  not not_1030 (not_1030_out, E);
  not not_1031 (not_1031_out, G);
  not not_1032 (not_1032_out, B);
  not not_1033 (not_1033_out, C);
  not not_1034 (not_1034_out, G);
  not not_1035 (not_1035_out, B);
  not not_1036 (not_1036_out, C);
  not not_1037 (not_1037_out, D);
  not not_1038 (not_1038_out, B);
  not not_1039 (not_1039_out, C);
  not not_1040 (not_1040_out, H);
  not not_1041 (not_1041_out, B);
  not not_1042 (not_1042_out, C);
  not not_1043 (not_1043_out, F);
  not not_1044 (not_1044_out, G);
  not not_1045 (not_1045_out, H);
  not not_1046 (not_1046_out, B);
  not not_1047 (not_1047_out, E);
  not not_1048 (not_1048_out, C);
  not not_1049 (not_1049_out, D);
  not not_1050 (not_1050_out, E);
  not not_1051 (not_1051_out, G);
  not not_1052 (not_1052_out, H);
  not not_1053 (not_1053_out, B);
  not not_1054 (not_1054_out, F);
  not not_1055 (not_1055_out, E);
  not not_1056 (not_1056_out, B);
  not not_1057 (not_1057_out, D);
  not not_1058 (not_1058_out, H);
  not not_1059 (not_1059_out, B);
  not not_1060 (not_1060_out, G);
  not not_1061 (not_1061_out, H);
  not not_1062 (not_1062_out, D);
  not not_1063 (not_1063_out, G);
  not not_1064 (not_1064_out, C);
  not not_1065 (not_1065_out, F);
  not not_1066 (not_1066_out, G);
  not not_1067 (not_1067_out, C);
  not not_1068 (not_1068_out, D);
  not not_1069 (not_1069_out, G);
  not not_1070 (not_1070_out, H);
  not not_1071 (not_1071_out, D);
  not not_1072 (not_1072_out, F);
  not not_1073 (not_1073_out, H);
  not not_1074 (not_1074_out, C);
  not not_1075 (not_1075_out, F);
  not not_1076 (not_1076_out, C);
  not not_1077 (not_1077_out, E);
  not not_1078 (not_1078_out, H);
  not not_1079 (not_1079_out, E);
  not not_1080 (not_1080_out, F);
  not not_1081 (not_1081_out, G);
  not not_1082 (not_1082_out, E);
  not not_1083 (not_1083_out, G);
  not not_1084 (not_1084_out, H);
  not not_1085 (not_1085_out, H);
  not not_1086 (not_1086_out, A);
  not not_1087 (not_1087_out, C);
  not not_1088 (not_1088_out, E);
  not not_1089 (not_1089_out, G);
  not not_1090 (not_1090_out, B);
  not not_1091 (not_1091_out, C);
  not not_1092 (not_1092_out, D);
  not not_1093 (not_1093_out, F);
  not not_1094 (not_1094_out, G);
  not not_1095 (not_1095_out, A);
  not not_1096 (not_1096_out, B);
  not not_1097 (not_1097_out, D);
  not not_1098 (not_1098_out, E);
  not not_1099 (not_1099_out, A);
  not not_1100 (not_1100_out, C);
  not not_1101 (not_1101_out, A);
  not not_1102 (not_1102_out, B);
  not not_1103 (not_1103_out, F);
  not not_1104 (not_1104_out, B);
  not not_1105 (not_1105_out, E);
  not not_1106 (not_1106_out, F);
  not not_1107 (not_1107_out, B);
  not not_1108 (not_1108_out, C);
  not not_1109 (not_1109_out, G);
  not not_1110 (not_1110_out, A);
  not not_1111 (not_1111_out, B);
  not not_1112 (not_1112_out, E);
  not not_1113 (not_1113_out, A);
  not not_1114 (not_1114_out, G);
  not not_1115 (not_1115_out, A);
  not not_1116 (not_1116_out, D);
  not not_1117 (not_1117_out, A);
  not not_1118 (not_1118_out, E);
  not not_1119 (not_1119_out, A);
  not not_1120 (not_1120_out, D);
  not not_1121 (not_1121_out, E);
  not not_1122 (not_1122_out, F);
  not not_1123 (not_1123_out, C);
  not not_1124 (not_1124_out, D);
  not not_1125 (not_1125_out, D);
  not not_1126 (not_1126_out, G);
  not not_1127 (not_1127_out, C);
  not not_1128 (not_1128_out, F);
  not not_1129 (not_1129_out, G);
  not not_1130 (not_1130_out, A);
  not not_1131 (not_1131_out, E);
  not not_1132 (not_1132_out, D);
  not not_1133 (not_1133_out, F);
  not not_1134 (not_1134_out, B);
  not not_1135 (not_1135_out, C);
  not not_1136 (not_1136_out, F);
  not not_1137 (not_1137_out, C);
  not not_1138 (not_1138_out, E);
  not not_1139 (not_1139_out, C);
  not not_1140 (not_1140_out, D);
  not not_1141 (not_1141_out, G);
  not not_1142 (not_1142_out, C);
  not not_1143 (not_1143_out, G);
  not not_1144 (not_1144_out, B);
  not not_1145 (not_1145_out, B);
  not not_1146 (not_1146_out, F);
  not not_1147 (not_1147_out, G);
  not not_1148 (not_1148_out, E);
  not not_1149 (not_1149_out, G);
  not not_1150 (not_1150_out, D);
  not not_1151 (not_1151_out, E);
  not not_1152 (not_1152_out, F);
  and and_1 (and_1_out, not_1_out, not_2_out, not_3_out, not_4_out, not_5_out);
  and and_2 (and_2_out, not_6_out, not_7_out, not_8_out, not_9_out, G);
  and and_3 (and_3_out, not_10_out, not_11_out, not_12_out, not_13_out, G, not_14_out);
  and and_4 (and_4_out, not_15_out, not_16_out, not_17_out, not_18_out, G);
  and and_5 (and_5_out, not_19_out, not_20_out, not_21_out, G, not_22_out);
  and and_6 (and_6_out, not_23_out, not_24_out, not_25_out, not_26_out, G, not_27_out);
  and and_7 (and_7_out, not_28_out, not_29_out, not_30_out, F, H);
  and and_8 (and_8_out, not_31_out, not_32_out, F, G, H);
  and and_9 (and_9_out, not_33_out, not_34_out, not_35_out, E, not_36_out);
  and and_10 (and_10_out, not_37_out, not_38_out, E, F, not_39_out);
  and and_11 (and_11_out, not_40_out, not_41_out, E, F, not_42_out, H);
  and and_12 (and_12_out, not_43_out, not_44_out, D, not_45_out, not_46_out, not_47_out);
  and and_13 (and_13_out, not_48_out, not_49_out, D, not_50_out, H);
  and and_14 (and_14_out, not_51_out, D, not_52_out, not_53_out, H);
  and and_15 (and_15_out, not_54_out, not_55_out, D, F, not_56_out);
  and and_16 (and_16_out, not_57_out, D, F, not_58_out, not_59_out);
  and and_17 (and_17_out, not_60_out, not_61_out, C, not_62_out, not_63_out);
  and and_18 (and_18_out, not_64_out, not_65_out, C, not_66_out, not_67_out, not_68_out);
  and and_19 (and_19_out, not_69_out, C, not_70_out, not_71_out, not_72_out);
  and and_20 (and_20_out, not_73_out, C, not_74_out, not_75_out, not_76_out, not_77_out);
  and and_21 (and_21_out, not_78_out, not_79_out, C, not_80_out, not_81_out, H);
  and and_22 (and_22_out, not_82_out, not_83_out, C, not_84_out, not_85_out, F);
  and and_23 (and_23_out, not_86_out, not_87_out, C, not_88_out, F, H);
  and and_24 (and_24_out, not_89_out, not_90_out, C, E, G);
  and and_25 (and_25_out, not_91_out, C, E, not_92_out, G);
  and and_26 (and_26_out, not_93_out, C, E, G, not_94_out);
  and and_27 (and_27_out, not_95_out, B, not_96_out, not_97_out, H);
  and and_28 (and_28_out, B, not_98_out, not_99_out, not_100_out, H);
  and and_29 (and_29_out, not_101_out, B, not_102_out, F, not_103_out);
  and and_30 (and_30_out, B, not_104_out, not_105_out, F, not_106_out, H);
  and and_31 (and_31_out, not_107_out, B, not_108_out, not_109_out, E, F);
  and and_32 (and_32_out, B, not_110_out, D, not_111_out, not_112_out);
  and and_33 (and_33_out, B, D, not_113_out, not_114_out, not_115_out);
  and and_34 (and_34_out, not_116_out, B, D, F, H);
  and and_35 (and_35_out, B, D, not_117_out, F, H);
  and and_36 (and_36_out, B, not_118_out, D, E, not_119_out, not_120_out);
  and and_37 (and_37_out, not_121_out, B, C, not_122_out, not_123_out, H);
  and and_38 (and_38_out, B, C, not_124_out, not_125_out, H);
  and and_39 (and_39_out, not_126_out, B, C, not_127_out, not_128_out, G);
  and and_40 (and_40_out, not_129_out, B, C, not_130_out, F, not_131_out);
  and and_41 (and_41_out, B, C, not_132_out, F, not_133_out);
  and and_42 (and_42_out, A, not_134_out, not_135_out, not_136_out, not_137_out, not_138_out);
  and and_43 (and_43_out, A, not_139_out, not_140_out, not_141_out, not_142_out);
  and and_44 (and_44_out, A, not_143_out, not_144_out, not_145_out, not_146_out);
  and and_45 (and_45_out, A, not_147_out, not_148_out, not_149_out, not_150_out, not_151_out);
  and and_46 (and_46_out, A, not_152_out, not_153_out, E, not_154_out, not_155_out);
  and and_47 (and_47_out, A, not_156_out, not_157_out, E, G);
  and and_48 (and_48_out, A, not_158_out, E, F, G);
  and and_49 (and_49_out, A, not_159_out, D, not_160_out, H);
  and and_50 (and_50_out, A, not_161_out, not_162_out, D, F, not_163_out);
  and and_51 (and_51_out, A, not_164_out, D, F, not_165_out);
  and and_52 (and_52_out, A, not_166_out, C, not_167_out, G);
  and and_53 (and_53_out, A, C, not_168_out, not_169_out, G);
  and and_54 (and_54_out, A, C, not_170_out, E, not_171_out);
  and and_55 (and_55_out, A, C, E, F, not_172_out);
  and and_56 (and_56_out, A, C, D, not_173_out, G);
  and and_57 (and_57_out, A, C, D, not_174_out, G, not_175_out);
  and and_58 (and_58_out, A, B, not_176_out, not_177_out, not_178_out);
  and and_59 (and_59_out, A, B, not_179_out, not_180_out, not_181_out, F);
  and and_60 (and_60_out, A, B, not_182_out, not_183_out, F, not_184_out);
  and and_61 (and_61_out, A, B, not_185_out, E, G);
  and and_62 (and_62_out, A, B, not_186_out, D, not_187_out, not_188_out);
  and and_63 (and_63_out, A, B, C, E, not_189_out);
  and and_64 (and_64_out, A, B, C, E, F, H);
  and and_65 (and_65_out, not_190_out, not_191_out, not_192_out, not_193_out, not_194_out, G);
  and and_66 (and_66_out, not_195_out, not_196_out, not_197_out, not_198_out, F, not_199_out);
  and and_67 (and_67_out, not_200_out, not_201_out, not_202_out, F, not_203_out);
  and and_68 (and_68_out, not_204_out, not_205_out, not_206_out, F, not_207_out);
  and and_69 (and_69_out, not_208_out, not_209_out, not_210_out, E, not_211_out);
  and and_70 (and_70_out, not_212_out, not_213_out, E, not_214_out, not_215_out);
  and and_71 (and_71_out, not_216_out, not_217_out, not_218_out, not_219_out, E, F);
  and and_72 (and_72_out, not_220_out, not_221_out, not_222_out, E, F, not_223_out);
  and and_73 (and_73_out, not_224_out, not_225_out, D, not_226_out, not_227_out);
  and and_74 (and_74_out, not_228_out, D, not_229_out, not_230_out, not_231_out);
  and and_75 (and_75_out, not_232_out, not_233_out, not_234_out, D, not_235_out, G);
  and and_76 (and_76_out, not_236_out, not_237_out, D, not_238_out, not_239_out, G);
  and and_77 (and_77_out, not_240_out, not_241_out, C, not_242_out, not_243_out, not_244_out);
  and and_78 (and_78_out, not_245_out, C, not_246_out, not_247_out, G);
  and and_79 (and_79_out, not_248_out, not_249_out, C, E, not_250_out, G);
  and and_80 (and_80_out, not_251_out, not_252_out, C, D, not_253_out, F);
  and and_81 (and_81_out, not_254_out, not_255_out, C, D, E, G);
  and and_82 (and_82_out, not_256_out, B, not_257_out, not_258_out, not_259_out, not_260_out);
  and and_83 (and_83_out, not_261_out, B, not_262_out, not_263_out, not_264_out);
  and and_84 (and_84_out, B, not_265_out, not_266_out, F, not_267_out, not_268_out);
  and and_85 (and_85_out, not_269_out, B, not_270_out, not_271_out, E, G);
  and and_86 (and_86_out, not_272_out, B, not_273_out, D, F, not_274_out);
  and and_87 (and_87_out, not_275_out, B, D, F, not_276_out);
  and and_88 (and_88_out, B, D, not_277_out, F, not_278_out);
  and and_89 (and_89_out, not_279_out, B, not_280_out, D, E, F);
  and and_90 (and_90_out, B, C, not_281_out, not_282_out, not_283_out);
  and and_91 (and_91_out, not_284_out, B, C, not_285_out, G);
  and and_92 (and_92_out, not_286_out, B, C, not_287_out, E, not_288_out);
  and and_93 (and_93_out, not_289_out, B, C, E, F, not_290_out);
  and and_94 (and_94_out, not_291_out, B, C, D, not_292_out, not_293_out);
  and and_95 (and_95_out, not_294_out, B, C, D, not_295_out, G);
  and and_96 (and_96_out, A, not_296_out, not_297_out, not_298_out, not_299_out);
  and and_97 (and_97_out, A, not_300_out, not_301_out, not_302_out, not_303_out, not_304_out);
  and and_98 (and_98_out, A, not_305_out, not_306_out, not_307_out, not_308_out);
  and and_99 (and_99_out, A, not_309_out, not_310_out, not_311_out, not_312_out, F);
  and and_100 (and_100_out, A, not_313_out, not_314_out, E, G);
  and and_101 (and_101_out, A, not_315_out, E, not_316_out, G);
  and and_102 (and_102_out, A, not_317_out, not_318_out, D, not_319_out, not_320_out);
  and and_103 (and_103_out, A, not_321_out, not_322_out, D, not_323_out, not_324_out);
  and and_104 (and_104_out, A, not_325_out, D, not_326_out, not_327_out);
  and and_105 (and_105_out, A, not_328_out, D, not_329_out, not_330_out, not_331_out);
  and and_106 (and_106_out, A, not_332_out, C, not_333_out, not_334_out, G);
  and and_107 (and_107_out, A, C, not_335_out, not_336_out, F, not_337_out);
  and and_108 (and_108_out, A, not_338_out, C, E, not_339_out);
  and and_109 (and_109_out, A, C, not_340_out, E, F, G);
  and and_110 (and_110_out, A, not_341_out, C, D, not_342_out, G);
  and and_111 (and_111_out, A, C, D, not_343_out, not_344_out, G);
  and and_112 (and_112_out, A, C, D, E, not_345_out);
  and and_113 (and_113_out, A, B, not_346_out, not_347_out, not_348_out, G);
  and and_114 (and_114_out, A, B, not_349_out, not_350_out, E, F, not_351_out);
  and and_115 (and_115_out, A, B, not_352_out, E, F, not_353_out);
  and and_116 (and_116_out, A, B, not_354_out, D, not_355_out, F);
  and and_117 (and_117_out, A, B, D, E, F, G);
  and and_118 (and_118_out, A, B, C, not_356_out, not_357_out, not_358_out);
  and and_119 (and_119_out, A, B, C, not_359_out, F, not_360_out);
  and and_120 (and_120_out, A, B, C, not_361_out, E, not_362_out);
  and and_121 (and_121_out, not_363_out, not_364_out, not_365_out, not_366_out, not_367_out);
  and and_122 (and_122_out, not_368_out, not_369_out, not_370_out, not_371_out, not_372_out, G);
  and and_123 (and_123_out, not_373_out, not_374_out, not_375_out, not_376_out, G, not_377_out);
  and and_124 (and_124_out, not_378_out, not_379_out, not_380_out, G, not_381_out);
  and and_125 (and_125_out, not_382_out, not_383_out, not_384_out, not_385_out, G, not_386_out);
  and and_126 (and_126_out, not_387_out, not_388_out, not_389_out, not_390_out, F, not_391_out, H);
  and and_127 (and_127_out, not_392_out, not_393_out, not_394_out, not_395_out, E, not_396_out);
  and and_128 (and_128_out, not_397_out, not_398_out, not_399_out, not_400_out, E, F, H);
  and and_129 (and_129_out, not_401_out, not_402_out, not_403_out, E, F, not_404_out, H);
  and and_130 (and_130_out, not_405_out, not_406_out, D, not_407_out, not_408_out, not_409_out);
  and and_131 (and_131_out, not_410_out, not_411_out, not_412_out, D, not_413_out, G);
  and and_132 (and_132_out, not_414_out, not_415_out, D, not_416_out, not_417_out, G);
  and and_133 (and_133_out, not_418_out, not_419_out, D, F, not_420_out);
  and and_134 (and_134_out, not_421_out, D, F, not_422_out, not_423_out);
  and and_135 (and_135_out, not_424_out, not_425_out, D, E, not_426_out, not_427_out, H);
  and and_136 (and_136_out, not_428_out, not_429_out, D, E, F, not_430_out);
  and and_137 (and_137_out, not_431_out, not_432_out, C, not_433_out, not_434_out, not_435_out);
  and and_138 (and_138_out, not_436_out, not_437_out, C, not_438_out, not_439_out, not_440_out);
  and and_139 (and_139_out, not_441_out, C, not_442_out, not_443_out, not_444_out);
  and and_140 (and_140_out, not_445_out, C, not_446_out, not_447_out, not_448_out, not_449_out);
  and and_141 (and_141_out, not_450_out, C, not_451_out, not_452_out, G, H);
  and and_142 (and_142_out, not_453_out, C, not_454_out, not_455_out, F, not_456_out);
  and and_143 (and_143_out, not_457_out, not_458_out, C, E, not_459_out, G);
  and and_144 (and_144_out, not_460_out, C, E, G, not_461_out);
  and and_145 (and_145_out, not_462_out, not_463_out, C, D, not_464_out, F, H);
  and and_146 (and_146_out, not_465_out, not_466_out, C, D, E, G);
  and and_147 (and_147_out, not_467_out, C, D, E, not_468_out, G);
  and and_148 (and_148_out, not_469_out, B, not_470_out, not_471_out, not_472_out, not_473_out, H);
  and and_149 (and_149_out, not_474_out, B, not_475_out, F, not_476_out);
  and and_150 (and_150_out, B, not_477_out, not_478_out, F, not_479_out);
  and and_151 (and_151_out, not_480_out, B, not_481_out, not_482_out, F, not_483_out, H);
  and and_152 (and_152_out, not_484_out, B, not_485_out, E, not_486_out, not_487_out);
  and and_153 (and_153_out, not_488_out, B, not_489_out, not_490_out, E, G, H);
  and and_154 (and_154_out, B, not_491_out, D, not_492_out, not_493_out);
  and and_155 (and_155_out, B, D, not_494_out, not_495_out, not_496_out);
  and and_156 (and_156_out, not_497_out, B, not_498_out, D, E, F, H);
  and and_157 (and_157_out, not_499_out, B, C, not_500_out, not_501_out, not_502_out);
  and and_158 (and_158_out, not_503_out, B, C, not_504_out, F, G);
  and and_159 (and_159_out, not_505_out, B, C, not_506_out, E, not_507_out, H);
  and and_160 (and_160_out, not_508_out, B, C, E, F, not_509_out, H);
  and and_161 (and_161_out, not_510_out, B, C, D, not_511_out, not_512_out, H);
  and and_162 (and_162_out, A, not_513_out, not_514_out, not_515_out, not_516_out, not_517_out);
  and and_163 (and_163_out, A, not_518_out, not_519_out, not_520_out, not_521_out);
  and and_164 (and_164_out, A, not_522_out, not_523_out, not_524_out, not_525_out, H);
  and and_165 (and_165_out, A, not_526_out, not_527_out, not_528_out, not_529_out, F, H);
  and and_166 (and_166_out, A, not_530_out, not_531_out, not_532_out, F, not_533_out, H);
  and and_167 (and_167_out, A, not_534_out, E, not_535_out, not_536_out, not_537_out);
  and and_168 (and_168_out, A, not_538_out, not_539_out, E, not_540_out, G);
  and and_169 (and_169_out, A, not_541_out, not_542_out, E, G, not_543_out);
  and and_170 (and_170_out, A, not_544_out, not_545_out, E, G, H);
  and and_171 (and_171_out, A, not_546_out, D, F, not_547_out);
  and and_172 (and_172_out, A, not_548_out, C, not_549_out, not_550_out, G);
  and and_173 (and_173_out, A, not_551_out, C, not_552_out, G, not_553_out);
  and and_174 (and_174_out, A, C, not_554_out, G, not_555_out);
  and and_175 (and_175_out, A, C, not_556_out, E, not_557_out, not_558_out);
  and and_176 (and_176_out, A, not_559_out, C, E, not_560_out, H);
  and and_177 (and_177_out, A, not_561_out, C, not_562_out, E, F, H);
  and and_178 (and_178_out, A, not_563_out, C, D, not_564_out, G);
  and and_179 (and_179_out, A, C, D, not_565_out, not_566_out, G);
  and and_180 (and_180_out, A, B, not_567_out, not_568_out, not_569_out, not_570_out);
  and and_181 (and_181_out, A, B, not_571_out, not_572_out, not_573_out, G, H);
  and and_182 (and_182_out, A, B, not_574_out, not_575_out, E, F, not_576_out, H);
  and and_183 (and_183_out, A, B, not_577_out, D, not_578_out, not_579_out);
  and and_184 (and_184_out, A, B, not_580_out, D, not_581_out, not_582_out);
  and and_185 (and_185_out, A, B, D, not_583_out, not_584_out);
  and and_186 (and_186_out, A, B, not_585_out, D, not_586_out, F, H);
  and and_187 (and_187_out, A, B, not_587_out, D, E, G);
  and and_188 (and_188_out, A, B, C, not_588_out, not_589_out, not_590_out, H);
  and and_189 (and_189_out, A, B, C, not_591_out, F, not_592_out, H);
  and and_190 (and_190_out, A, B, C, not_593_out, E, not_594_out, H);
  and and_191 (and_191_out, A, B, C, not_595_out, E, F, G);
  and and_192 (and_192_out, A, B, C, D, E, not_596_out);
  and and_193 (and_193_out, A, B, C, D, E, F, H);
  and and_194 (and_194_out, not_597_out, not_598_out, not_599_out, not_600_out, not_601_out);
  and and_195 (and_195_out, not_602_out, not_603_out, not_604_out, not_605_out, F, not_606_out);
  and and_196 (and_196_out, not_607_out, not_608_out, not_609_out, not_610_out, F, not_611_out);
  and and_197 (and_197_out, not_612_out, not_613_out, not_614_out, E, not_615_out, not_616_out);
  and and_198 (and_198_out, not_617_out, not_618_out, E, G, not_619_out);
  and and_199 (and_199_out, not_620_out, not_621_out, not_622_out, E, F, G);
  and and_200 (and_200_out, not_623_out, not_624_out, D, not_625_out, not_626_out);
  and and_201 (and_201_out, not_627_out, not_628_out, not_629_out, D, not_630_out, not_631_out, G);
  and and_202 (and_202_out, not_632_out, not_633_out, D, F, not_634_out, not_635_out);
  and and_203 (and_203_out, not_636_out, not_637_out, not_638_out, D, E, not_639_out);
  and and_204 (and_204_out, not_640_out, not_641_out, D, E, not_642_out, not_643_out);
  and and_205 (and_205_out, not_644_out, not_645_out, C, not_646_out, not_647_out, G);
  and and_206 (and_206_out, not_648_out, C, not_649_out, F, G, not_650_out);
  and and_207 (and_207_out, not_651_out, C, E, not_652_out, not_653_out);
  and and_208 (and_208_out, not_654_out, C, not_655_out, E, F, not_656_out);
  and and_209 (and_209_out, not_657_out, not_658_out, C, D, not_659_out, not_660_out, not_661_out);
  and and_210 (and_210_out, not_662_out, C, D, not_663_out, F, G);
  and and_211 (and_211_out, not_664_out, not_665_out, C, D, E, not_666_out, G);
  and and_212 (and_212_out, not_667_out, B, not_668_out, not_669_out, not_670_out, not_671_out);
  and and_213 (and_213_out, not_672_out, B, not_673_out, not_674_out, not_675_out, not_676_out);
  and and_214 (and_214_out, not_677_out, B, not_678_out, not_679_out, F, not_680_out);
  and and_215 (and_215_out, B, not_681_out, not_682_out, F, not_683_out);
  and and_216 (and_216_out, B, not_684_out, F, not_685_out, not_686_out);
  and and_217 (and_217_out, not_687_out, B, not_688_out, not_689_out, E, G);
  and and_218 (and_218_out, not_690_out, B, not_691_out, E, F, G);
  and and_219 (and_219_out, not_692_out, B, D, not_693_out, F, not_694_out);
  and and_220 (and_220_out, not_695_out, B, C, not_696_out, not_697_out, G);
  and and_221 (and_221_out, not_698_out, B, C, not_699_out, E, not_700_out);
  and and_222 (and_222_out, not_701_out, B, C, not_702_out, E, not_703_out);
  and and_223 (and_223_out, not_704_out, B, C, E, F, not_705_out);
  and and_224 (and_224_out, B, C, D, F, G, not_706_out);
  and and_225 (and_225_out, A, not_707_out, not_708_out, not_709_out, not_710_out, not_711_out);
  and and_226 (and_226_out, A, not_712_out, not_713_out, G, not_714_out);
  and and_227 (and_227_out, A, not_715_out, not_716_out, not_717_out, F, G);
  and and_228 (and_228_out, A, not_718_out, not_719_out, E, not_720_out, not_721_out);
  and and_229 (and_229_out, A, not_722_out, not_723_out, E, not_724_out, G);
  and and_230 (and_230_out, A, not_725_out, not_726_out, D, not_727_out, not_728_out);
  and and_231 (and_231_out, A, not_729_out, D, not_730_out, not_731_out, not_732_out);
  and and_232 (and_232_out, A, not_733_out, not_734_out, D, E, G);
  and and_233 (and_233_out, A, not_735_out, D, E, not_736_out, G);
  and and_234 (and_234_out, A, C, not_737_out, not_738_out, not_739_out);
  and and_235 (and_235_out, A, C, not_740_out, not_741_out, F, not_742_out);
  and and_236 (and_236_out, A, not_743_out, C, E, not_744_out, not_745_out);
  and and_237 (and_237_out, A, C, E, G, not_746_out);
  and and_238 (and_238_out, A, C, not_747_out, E, F, G);
  and and_239 (and_239_out, A, not_748_out, C, D, not_749_out, not_750_out, G);
  and and_240 (and_240_out, A, not_751_out, C, D, E, not_752_out);
  and and_241 (and_241_out, A, C, D, E, not_753_out, not_754_out);
  and and_242 (and_242_out, A, B, not_755_out, not_756_out, not_757_out, G);
  and and_243 (and_243_out, A, B, not_758_out, not_759_out, F, G);
  and and_244 (and_244_out, A, B, not_760_out, E, not_761_out, not_762_out);
  and and_245 (and_245_out, A, B, not_763_out, not_764_out, E, F, not_765_out);
  and and_246 (and_246_out, A, B, C, not_766_out, not_767_out, not_768_out);
  and and_247 (and_247_out, A, B, C, not_769_out, not_770_out, not_771_out);
  and and_248 (and_248_out, A, B, C, not_772_out, F, not_773_out);
  and and_249 (and_249_out, A, B, C, not_774_out, E, G);
  and and_250 (and_250_out, A, B, C, E, F, G);
  and and_251 (and_251_out, not_775_out, not_776_out, not_777_out, not_778_out, not_779_out);
  and and_252 (and_252_out, not_780_out, not_781_out, not_782_out, not_783_out, G, not_784_out);
  and and_253 (and_253_out, not_785_out, not_786_out, not_787_out, G, not_788_out);
  and and_254 (and_254_out, not_789_out, not_790_out, not_791_out, not_792_out, G, not_793_out);
  and and_255 (and_255_out, not_794_out, not_795_out, not_796_out, E, not_797_out, not_798_out);
  and and_256 (and_256_out, not_799_out, not_800_out, D, not_801_out, not_802_out, not_803_out);
  and and_257 (and_257_out, not_804_out, not_805_out, D, F, not_806_out);
  and and_258 (and_258_out, not_807_out, D, F, not_808_out, not_809_out);
  and and_259 (and_259_out, not_810_out, not_811_out, C, not_812_out, not_813_out, not_814_out);
  and and_260 (and_260_out, not_815_out, C, not_816_out, not_817_out, not_818_out);
  and and_261 (and_261_out, not_819_out, C, not_820_out, not_821_out, not_822_out, not_823_out);
  and and_262 (and_262_out, not_824_out, C, not_825_out, not_826_out, F, not_827_out);
  and and_263 (and_263_out, not_828_out, C, E, G, not_829_out);
  and and_264 (and_264_out, not_830_out, B, not_831_out, F, not_832_out);
  and and_265 (and_265_out, B, not_833_out, not_834_out, F, not_835_out);
  and and_266 (and_266_out, not_836_out, B, not_837_out, E, not_838_out, not_839_out);
  and and_267 (and_267_out, B, not_840_out, D, not_841_out, not_842_out);
  and and_268 (and_268_out, B, D, not_843_out, not_844_out, not_845_out);
  and and_269 (and_269_out, not_846_out, B, C, not_847_out, not_848_out, not_849_out);
  and and_270 (and_270_out, not_850_out, B, C, not_851_out, F, not_852_out);
  and and_271 (and_271_out, B, C, not_853_out, F, not_854_out);
  and and_272 (and_272_out, A, not_855_out, not_856_out, not_857_out, not_858_out, not_859_out);
  and and_273 (and_273_out, A, not_860_out, not_861_out, not_862_out, not_863_out);
  and and_274 (and_274_out, A, not_864_out, not_865_out, not_866_out, not_867_out, not_868_out);
  and and_275 (and_275_out, A, not_869_out, not_870_out, E, not_871_out, not_872_out);
  and and_276 (and_276_out, A, not_873_out, not_874_out, E, G, not_875_out);
  and and_277 (and_277_out, A, not_876_out, D, F, not_877_out);
  and and_278 (and_278_out, A, not_878_out, C, not_879_out, G, not_880_out);
  and and_279 (and_279_out, A, C, not_881_out, G, not_882_out);
  and and_280 (and_280_out, A, C, not_883_out, E, not_884_out, not_885_out);
  and and_281 (and_281_out, A, B, not_886_out, D, not_887_out, not_888_out);
  and and_282 (and_282_out, A, B, D, not_889_out, not_890_out);
  and and_283 (and_283_out, A, B, not_891_out, D, E, not_892_out);
  and and_284 (and_284_out, A, B, C, E, not_893_out, not_894_out);
  and and_285 (and_285_out, not_895_out, not_896_out, not_897_out, not_898_out, not_899_out);
  and and_286 (and_286_out, not_900_out, not_901_out, not_902_out, not_903_out, not_904_out, H);
  and and_287 (and_287_out, not_905_out, not_906_out, not_907_out, not_908_out, G, H);
  and and_288 (and_288_out, not_909_out, not_910_out, not_911_out, G, H);
  and and_289 (and_289_out, not_912_out, not_913_out, not_914_out, not_915_out, G, H);
  and and_290 (and_290_out, not_916_out, not_917_out, not_918_out, F, not_919_out, not_920_out);
  and and_291 (and_291_out, not_921_out, not_922_out, not_923_out, E, not_924_out, not_925_out);
  and and_292 (and_292_out, not_926_out, not_927_out, not_928_out, E, not_929_out, H);
  and and_293 (and_293_out, not_930_out, not_931_out, not_932_out, E, G, not_933_out);
  and and_294 (and_294_out, not_934_out, not_935_out, D, not_936_out, not_937_out, G);
  and and_295 (and_295_out, not_938_out, not_939_out, not_940_out, D, F);
  and and_296 (and_296_out, not_941_out, not_942_out, D, F, not_943_out);
  and and_297 (and_297_out, not_944_out, not_945_out, C, not_946_out, not_947_out, not_948_out);
  and and_298 (and_298_out, not_949_out, not_950_out, C, not_951_out, not_952_out, H);
  and and_299 (and_299_out, not_953_out, C, not_954_out, not_955_out, H);
  and and_300 (and_300_out, not_956_out, C, not_957_out, not_958_out, not_959_out, H);
  and and_301 (and_301_out, not_960_out, not_961_out, C, not_962_out, G, not_963_out);
  and and_302 (and_302_out, not_964_out, C, not_965_out, G, not_966_out);
  and and_303 (and_303_out, not_967_out, C, not_968_out, not_969_out, G, not_970_out);
  and and_304 (and_304_out, not_971_out, C, not_972_out, not_973_out, F, G);
  and and_305 (and_305_out, not_974_out, C, not_975_out, E, not_976_out, not_977_out);
  and and_306 (and_306_out, not_978_out, C, not_979_out, E, not_980_out);
  and and_307 (and_307_out, not_981_out, C, E, G, H);
  and and_308 (and_308_out, not_982_out, C, D, E, F);
  and and_309 (and_309_out, B, not_983_out, not_984_out, not_985_out, not_986_out, not_987_out);
  and and_310 (and_310_out, not_988_out, B, not_989_out, not_990_out, F);
  and and_311 (and_311_out, not_991_out, B, not_992_out, F, H);
  and and_312 (and_312_out, B, not_993_out, not_994_out, F, H);
  and and_313 (and_313_out, B, not_995_out, F, G, H);
  and and_314 (and_314_out, not_996_out, B, not_997_out, D, not_998_out);
  and and_315 (and_315_out, not_999_out, B, D, not_1000_out, not_1001_out);
  and and_316 (and_316_out, B, not_1002_out, D, F, not_1003_out, not_1004_out);
  and and_317 (and_317_out, not_1005_out, B, not_1006_out, D, E, not_1007_out);
  and and_318 (and_318_out, not_1008_out, B, not_1009_out, D, E, not_1010_out);
  and and_319 (and_319_out, not_1011_out, B, C, not_1012_out, not_1013_out, G);
  and and_320 (and_320_out, not_1014_out, B, C, not_1015_out, F, G);
  and and_321 (and_321_out, B, C, not_1016_out, F, G);
  and and_322 (and_322_out, not_1017_out, B, C, E, not_1018_out, not_1019_out);
  and and_323 (and_323_out, B, C, D, E, not_1020_out);
  and and_324 (and_324_out, A, not_1021_out, not_1022_out, not_1023_out, not_1024_out);
  and and_325 (and_325_out, A, not_1025_out, not_1026_out, not_1027_out, G, not_1028_out);
  and and_326 (and_326_out, A, not_1029_out, not_1030_out, F, not_1031_out, H);
  and and_327 (and_327_out, A, not_1032_out, not_1033_out, E, not_1034_out, H);
  and and_328 (and_328_out, A, not_1035_out, not_1036_out, not_1037_out, E, G);
  and and_329 (and_329_out, A, not_1038_out, not_1039_out, E, G, not_1040_out);
  and and_330 (and_330_out, A, not_1041_out, not_1042_out, D, not_1043_out, not_1044_out, not_1045_out);
  and and_331 (and_331_out, A, not_1046_out, D, not_1047_out, F);
  and and_332 (and_332_out, A, not_1048_out, D, E, F, G);
  and and_333 (and_333_out, A, C, not_1049_out, not_1050_out, not_1051_out, not_1052_out);
  and and_334 (and_334_out, A, not_1053_out, C, not_1054_out, G, H);
  and and_335 (and_335_out, A, C, not_1055_out, G, H);
  and and_336 (and_336_out, A, not_1056_out, C, not_1057_out, E, not_1058_out);
  and and_337 (and_337_out, A, not_1059_out, C, E, not_1060_out, not_1061_out);
  and and_338 (and_338_out, A, C, not_1062_out, E, not_1063_out, H);
  and and_339 (and_339_out, A, B, not_1064_out, not_1065_out, not_1066_out, H);
  and and_340 (and_340_out, A, B, not_1067_out, not_1068_out, E, not_1069_out, not_1070_out);
  and and_341 (and_341_out, A, B, not_1071_out, E, not_1072_out, not_1073_out);
  and and_342 (and_342_out, A, B, not_1074_out, E, not_1075_out, G);
  and and_343 (and_343_out, A, B, not_1076_out, D, not_1077_out, not_1078_out);
  and and_344 (and_344_out, A, B, D, not_1079_out, not_1080_out);
  and and_345 (and_345_out, A, B, D, E, F, not_1081_out);
  and and_346 (and_346_out, A, B, C, not_1082_out, not_1083_out, not_1084_out);
  and and_347 (and_347_out, A, B, C, D, E, not_1085_out);
  and and_348 (and_348_out, not_1086_out, not_1087_out, not_1088_out, not_1089_out);
  and and_349 (and_349_out, not_1090_out, not_1091_out, not_1092_out, not_1093_out, not_1094_out);
  and and_350 (and_350_out, not_1095_out, not_1096_out, not_1097_out, not_1098_out, F);
  and and_351 (and_351_out, not_1099_out, not_1100_out, E, G);
  and and_352 (and_352_out, not_1101_out, not_1102_out, D, not_1103_out);
  and and_353 (and_353_out, not_1104_out, D, not_1105_out, not_1106_out);
  and and_354 (and_354_out, not_1107_out, not_1108_out, D, F, not_1109_out);
  and and_355 (and_355_out, not_1110_out, not_1111_out, C, not_1112_out, G);
  and and_356 (and_356_out, not_1113_out, C, E, not_1114_out);
  and and_357 (and_357_out, not_1115_out, C, not_1116_out, E, F);
  and and_358 (and_358_out, not_1117_out, C, D, not_1118_out, G);
  and and_359 (and_359_out, not_1119_out, B, not_1120_out, not_1121_out, not_1122_out);
  and and_360 (and_360_out, B, not_1123_out, not_1124_out, F);
  and and_361 (and_361_out, B, not_1125_out, F, not_1126_out);
  and and_362 (and_362_out, B, not_1127_out, D, not_1128_out, not_1129_out);
  and and_363 (and_363_out, not_1130_out, B, D, not_1131_out, F);
  and and_364 (and_364_out, B, C, not_1132_out, not_1133_out, G);
  and and_365 (and_365_out, B, C, D, F, G);
  and and_366 (and_366_out, A, not_1134_out, not_1135_out, not_1136_out, G);
  and and_367 (and_367_out, A, not_1137_out, not_1138_out, G);
  and and_368 (and_368_out, A, not_1139_out, not_1140_out, E, not_1141_out);
  and and_369 (and_369_out, A, not_1142_out, E, F, not_1143_out);
  and and_370 (and_370_out, A, not_1144_out, D, E, F);
  and and_371 (and_371_out, A, not_1145_out, C, not_1146_out, not_1147_out);
  and and_372 (and_372_out, A, C, not_1148_out, not_1149_out);
  and and_373 (and_373_out, A, C, not_1150_out, not_1151_out, F);
  and and_374 (and_374_out, A, C, E, G);
  and and_375 (and_375_out, A, B, D, E, not_1152_out);
  or or_1 (or_1_out, and_251_out, and_252_out, and_253_out, and_254_out, and_255_out, and_256_out, and_257_out, and_258_out, and_259_out, and_260_out, and_261_out, and_262_out, and_263_out, and_264_out, and_265_out, and_266_out, and_267_out);
  or or_2 (or_2_out, and_268_out, and_269_out, and_270_out, and_271_out, and_272_out, and_273_out, and_274_out, and_275_out, and_276_out, and_277_out, and_278_out, and_279_out, and_280_out, and_281_out, and_282_out, and_283_out, and_284_out);
  or or_3 (or_3_out, and_1_out, and_2_out, and_3_out, and_4_out, and_5_out, and_6_out, and_7_out, and_8_out, and_9_out, and_10_out, and_11_out, and_12_out, and_13_out, and_14_out, and_15_out, and_16_out, and_17_out, and_18_out, and_19_out, and_20_out, and_21_out, and_22_out, and_23_out, and_24_out, and_25_out, and_26_out, and_27_out, and_28_out, and_29_out, and_30_out, and_31_out, and_32_out);
  or or_4 (or_4_out, and_33_out, and_34_out, and_35_out, and_36_out, and_37_out, and_38_out, and_39_out, and_40_out, and_41_out, and_42_out, and_43_out, and_44_out, and_45_out, and_46_out, and_47_out, and_48_out, and_49_out, and_50_out, and_51_out, and_52_out, and_53_out, and_54_out, and_55_out, and_56_out, and_57_out, and_58_out, and_59_out, and_60_out, and_61_out, and_62_out, and_63_out, and_64_out);
  or or_5 (or_5_out, and_65_out, and_66_out, and_67_out, and_68_out, and_69_out, and_70_out, and_71_out, and_72_out, and_73_out, and_74_out, and_75_out, and_76_out, and_77_out, and_78_out, and_79_out, and_80_out, and_81_out, and_82_out, and_83_out, and_84_out, and_85_out, and_86_out, and_87_out, and_88_out, and_89_out, and_90_out, and_91_out, and_92_out);
  or or_6 (or_6_out, and_93_out, and_94_out, and_95_out, and_96_out, and_97_out, and_98_out, and_99_out, and_100_out, and_101_out, and_102_out, and_103_out, and_104_out, and_105_out, and_106_out, and_107_out, and_108_out, and_109_out, and_110_out, and_111_out, and_112_out, and_113_out, and_114_out, and_115_out, and_116_out, and_117_out, and_118_out, and_119_out, and_120_out);
  or or_7 (or_7_out, and_121_out, and_122_out, and_123_out, and_124_out, and_125_out, and_126_out, and_127_out, and_128_out, and_129_out, and_130_out, and_131_out, and_132_out, and_133_out, and_134_out, and_135_out, and_136_out, and_137_out, and_138_out, and_139_out, and_140_out, and_141_out, and_142_out, and_143_out, and_144_out, and_145_out);
  or or_8 (or_8_out, and_146_out, and_147_out, and_148_out, and_149_out, and_150_out, and_151_out, and_152_out, and_153_out, and_154_out, and_155_out, and_156_out, and_157_out, and_158_out, and_159_out, and_160_out, and_161_out, and_162_out, and_163_out, and_164_out, and_165_out, and_166_out, and_167_out, and_168_out, and_169_out);
  or or_9 (or_9_out, and_170_out, and_171_out, and_172_out, and_173_out, and_174_out, and_175_out, and_176_out, and_177_out, and_178_out, and_179_out, and_180_out, and_181_out, and_182_out, and_183_out, and_184_out, and_185_out, and_186_out, and_187_out, and_188_out, and_189_out, and_190_out, and_191_out, and_192_out, and_193_out);
  or or_10 (or_10_out, and_194_out, and_195_out, and_196_out, and_197_out, and_198_out, and_199_out, and_200_out, and_201_out, and_202_out, and_203_out, and_204_out, and_205_out, and_206_out, and_207_out, and_208_out, and_209_out, and_210_out, and_211_out, and_212_out, and_213_out, and_214_out, and_215_out, and_216_out, and_217_out, and_218_out, and_219_out, and_220_out, and_221_out, and_222_out);
  or or_11 (or_11_out, and_223_out, and_224_out, and_225_out, and_226_out, and_227_out, and_228_out, and_229_out, and_230_out, and_231_out, and_232_out, and_233_out, and_234_out, and_235_out, and_236_out, and_237_out, and_238_out, and_239_out, and_240_out, and_241_out, and_242_out, and_243_out, and_244_out, and_245_out, and_246_out, and_247_out, and_248_out, and_249_out, and_250_out);
  or or_12 (LeftBottom, or_1_out, or_2_out);
  or or_13 (or_13_out, and_285_out, and_286_out, and_287_out, and_288_out, and_289_out, and_290_out, and_291_out, and_292_out, and_293_out, and_294_out, and_295_out, and_296_out, and_297_out, and_298_out, and_299_out, and_300_out, and_301_out, and_302_out, and_303_out, and_304_out, and_305_out, and_306_out, and_307_out, and_308_out, and_309_out, and_310_out, and_311_out, and_312_out, and_313_out, and_314_out, and_315_out, and_316_out);
  or or_14 (or_14_out, and_317_out, and_318_out, and_319_out, and_320_out, and_321_out, and_322_out, and_323_out, and_324_out, and_325_out, and_326_out, and_327_out, and_328_out, and_329_out, and_330_out, and_331_out, and_332_out, and_333_out, and_334_out, and_335_out, and_336_out, and_337_out, and_338_out, and_339_out, and_340_out, and_341_out, and_342_out, and_343_out, and_344_out, and_345_out, and_346_out, and_347_out);
  or or_15 (RightBottom, and_348_out, and_349_out, H, and_350_out, and_351_out, and_352_out, and_353_out, and_354_out, and_355_out, and_356_out, and_357_out, and_358_out, and_359_out, and_360_out, and_361_out, and_362_out, and_363_out, and_364_out, and_365_out, and_366_out, and_367_out, and_368_out, and_369_out, and_370_out, and_371_out, and_372_out, and_373_out, and_374_out, and_375_out);
  or or_16 (Top, or_3_out, or_4_out);
  or or_17 (Middle, or_5_out, or_6_out);
  or or_18 (Bottom, or_7_out, or_8_out, or_9_out);
  or or_19 (LeftTop, or_10_out, or_11_out);
  or or_20 (RightTop, or_13_out, or_14_out);
endmodule
// Display 2
module _2_Display (
  input  A,
  input  B,
  input  C,
  input  D,
  input  E,
  input  F,
  input  G,
  output Top,
  output Middle,
  output Bottom,
  output LeftTop,
  output LeftBottom,
  output RightTop,
  output RightBottom
);

  wire and_1_out, and_2_out, and_3_out, and_4_out, and_5_out, and_6_out, and_7_out, and_8_out, and_9_out,
       and_10_out, and_11_out, and_12_out, and_13_out, and_14_out, and_15_out, and_16_out, and_17_out,
       and_18_out, and_19_out, and_20_out, and_21_out, and_22_out, and_23_out, and_24_out, and_25_out,
       and_26_out, and_27_out, and_28_out, and_29_out, and_30_out, and_31_out, and_32_out, and_33_out,
       and_34_out, and_35_out, and_36_out, and_37_out, and_38_out, and_39_out, and_40_out, and_41_out,
       and_42_out, and_43_out, and_44_out, and_45_out, and_46_out, and_47_out, and_48_out, and_49_out,
       and_50_out, and_51_out, and_52_out, and_53_out, and_54_out, and_55_out, and_56_out, and_57_out,
       and_58_out, and_59_out, and_60_out, and_61_out, and_62_out, and_63_out, and_64_out, and_65_out,
       and_66_out, and_67_out, and_68_out, and_69_out, and_70_out, and_71_out, and_72_out, and_73_out,
       and_74_out, and_75_out, and_76_out, and_77_out, and_78_out, and_79_out, and_80_out, and_81_out,
       and_82_out, and_83_out, and_84_out, and_85_out, and_86_out, and_87_out, and_88_out, and_89_out,
       and_90_out, and_91_out, and_92_out, and_93_out, and_94_out, and_95_out, and_96_out, and_97_out,
       and_98_out, and_99_out, and_100_out, and_101_out, and_102_out, and_103_out, and_104_out, and_105_out,
       and_106_out, and_107_out, and_108_out, and_109_out, and_110_out, and_111_out, and_112_out,
       and_113_out, and_114_out, and_115_out, and_116_out, not_1_out, not_2_out, not_3_out, not_4_out,
       not_5_out, not_6_out, not_7_out, not_8_out, not_9_out, not_10_out, not_11_out, not_12_out, not_13_out,
       not_14_out, not_15_out, not_16_out, not_17_out, not_18_out, not_19_out, not_20_out, not_21_out,
       not_22_out, not_23_out, not_24_out, not_25_out, not_26_out, not_27_out, not_28_out, not_29_out,
       not_30_out, not_31_out, not_32_out, not_33_out, not_34_out, not_35_out, not_36_out, not_37_out,
       not_38_out, not_39_out, not_40_out, not_41_out, not_42_out, not_43_out, not_44_out, not_45_out,
       not_46_out, not_47_out, not_48_out, not_49_out, not_50_out, not_51_out, not_52_out, not_53_out,
       not_54_out, not_55_out, not_56_out, not_57_out, not_58_out, not_59_out, not_60_out, not_61_out,
       not_62_out, not_63_out, not_64_out, not_65_out, not_66_out, not_67_out, not_68_out, not_69_out,
       not_70_out, not_71_out, not_72_out, not_73_out, not_74_out, not_75_out, not_76_out, not_77_out,
       not_78_out, not_79_out, not_80_out, not_81_out, not_82_out, not_83_out, not_84_out, not_85_out,
       not_86_out, not_87_out, not_88_out, not_89_out, not_90_out, not_91_out, not_92_out, not_93_out,
       not_94_out, not_95_out, not_96_out, not_97_out, not_98_out, not_99_out, not_100_out, not_101_out,
       not_102_out, not_103_out, not_104_out, not_105_out, not_106_out, not_107_out, not_108_out,
       not_109_out, not_110_out, not_111_out, not_112_out, not_113_out, not_114_out, not_115_out,
       not_116_out, not_117_out, not_118_out, not_119_out, not_120_out, not_121_out, not_122_out,
       not_123_out, not_124_out, not_125_out, not_126_out, not_127_out, not_128_out, not_129_out,
       not_130_out, not_131_out, not_132_out, not_133_out, not_134_out, not_135_out, not_136_out,
       not_137_out, not_138_out, not_139_out, not_140_out, not_141_out, not_142_out, not_143_out,
       not_144_out, not_145_out, not_146_out, not_147_out, not_148_out, not_149_out, not_150_out,
       not_151_out, not_152_out, not_153_out, not_154_out, not_155_out, not_156_out, not_157_out,
       not_158_out, not_159_out, not_160_out, not_161_out, not_162_out, not_163_out, not_164_out,
       not_165_out, not_166_out, not_167_out, not_168_out, not_169_out, not_170_out, not_171_out,
       not_172_out, not_173_out, not_174_out, not_175_out, not_176_out, not_177_out, not_178_out,
       not_179_out, not_180_out, not_181_out, not_182_out, not_183_out, not_184_out, not_185_out,
       not_186_out, not_187_out, not_188_out, not_189_out, not_190_out, not_191_out, not_192_out,
       not_193_out, not_194_out, not_195_out, not_196_out, not_197_out, not_198_out, not_199_out,
       not_200_out, not_201_out, not_202_out, not_203_out, not_204_out, not_205_out, not_206_out,
       not_207_out, not_208_out, not_209_out, not_210_out, not_211_out, not_212_out, not_213_out,
       not_214_out, not_215_out, not_216_out, not_217_out, not_218_out, not_219_out, not_220_out,
       not_221_out, not_222_out, not_223_out, not_224_out, not_225_out, not_226_out, not_227_out,
       not_228_out, not_229_out, not_230_out, not_231_out, not_232_out, not_233_out, not_234_out,
       not_235_out, not_236_out, not_237_out, not_238_out, not_239_out, not_240_out, not_241_out,
       not_242_out, not_243_out, not_244_out, not_245_out, not_246_out, not_247_out, not_248_out,
       not_249_out, not_250_out, not_251_out, not_252_out, not_253_out, not_254_out, not_255_out,
       not_256_out, not_257_out, not_258_out, not_259_out, not_260_out, not_261_out, not_262_out,
       not_263_out, not_264_out, not_265_out, not_266_out, not_267_out, not_268_out;

  not not_1 (not_1_out, C);
  not not_2 (not_2_out, D);
  not not_3 (not_3_out, F);
  not not_4 (not_4_out, G);
  not not_5 (not_5_out, D);
  not not_6 (not_6_out, E);
  not not_7 (not_7_out, A);
  not not_8 (not_8_out, B);
  not not_9 (not_9_out, E);
  not not_10 (not_10_out, B);
  not not_11 (not_11_out, E);
  not not_12 (not_12_out, B);
  not not_13 (not_13_out, B);
  not not_14 (not_14_out, E);
  not not_15 (not_15_out, A);
  not not_16 (not_16_out, C);
  not not_17 (not_17_out, C);
  not not_18 (not_18_out, E);
  not not_19 (not_19_out, F);
  not not_20 (not_20_out, G);
  not not_21 (not_21_out, D);
  not not_22 (not_22_out, G);
  not not_23 (not_23_out, A);
  not not_24 (not_24_out, F);
  not not_25 (not_25_out, D);
  not not_26 (not_26_out, F);
  not not_27 (not_27_out, B);
  not not_28 (not_28_out, D);
  not not_29 (not_29_out, B);
  not not_30 (not_30_out, A);
  not not_31 (not_31_out, B);
  not not_32 (not_32_out, A);
  not not_33 (not_33_out, B);
  not not_34 (not_34_out, C);
  not not_35 (not_35_out, D);
  not not_36 (not_36_out, E);
  not not_37 (not_37_out, G);
  not not_38 (not_38_out, D);
  not not_39 (not_39_out, E);
  not not_40 (not_40_out, F);
  not not_41 (not_41_out, A);
  not not_42 (not_42_out, C);
  not not_43 (not_43_out, B);
  not not_44 (not_44_out, C);
  not not_45 (not_45_out, B);
  not not_46 (not_46_out, D);
  not not_47 (not_47_out, F);
  not not_48 (not_48_out, G);
  not not_49 (not_49_out, D);
  not not_50 (not_50_out, E);
  not not_51 (not_51_out, B);
  not not_52 (not_52_out, C);
  not not_53 (not_53_out, D);
  not not_54 (not_54_out, F);
  not not_55 (not_55_out, G);
  not not_56 (not_56_out, B);
  not not_57 (not_57_out, D);
  not not_58 (not_58_out, E);
  not not_59 (not_59_out, D);
  not not_60 (not_60_out, E);
  not not_61 (not_61_out, F);
  not not_62 (not_62_out, D);
  not not_63 (not_63_out, E);
  not not_64 (not_64_out, G);
  not not_65 (not_65_out, A);
  not not_66 (not_66_out, B);
  not not_67 (not_67_out, E);
  not not_68 (not_68_out, B);
  not not_69 (not_69_out, E);
  not not_70 (not_70_out, B);
  not not_71 (not_71_out, D);
  not not_72 (not_72_out, E);
  not not_73 (not_73_out, A);
  not not_74 (not_74_out, B);
  not not_75 (not_75_out, E);
  not not_76 (not_76_out, B);
  not not_77 (not_77_out, E);
  not not_78 (not_78_out, C);
  not not_79 (not_79_out, E);
  not not_80 (not_80_out, F);
  not not_81 (not_81_out, G);
  not not_82 (not_82_out, A);
  not not_83 (not_83_out, C);
  not not_84 (not_84_out, D);
  not not_85 (not_85_out, G);
  not not_86 (not_86_out, A);
  not not_87 (not_87_out, F);
  not not_88 (not_88_out, C);
  not not_89 (not_89_out, D);
  not not_90 (not_90_out, F);
  not not_91 (not_91_out, D);
  not not_92 (not_92_out, F);
  not not_93 (not_93_out, G);
  not not_94 (not_94_out, D);
  not not_95 (not_95_out, A);
  not not_96 (not_96_out, B);
  not not_97 (not_97_out, C);
  not not_98 (not_98_out, D);
  not not_99 (not_99_out, E);
  not not_100 (not_100_out, A);
  not not_101 (not_101_out, B);
  not not_102 (not_102_out, C);
  not not_103 (not_103_out, D);
  not not_104 (not_104_out, F);
  not not_105 (not_105_out, G);
  not not_106 (not_106_out, A);
  not not_107 (not_107_out, C);
  not not_108 (not_108_out, D);
  not not_109 (not_109_out, E);
  not not_110 (not_110_out, F);
  not not_111 (not_111_out, A);
  not not_112 (not_112_out, C);
  not not_113 (not_113_out, D);
  not not_114 (not_114_out, E);
  not not_115 (not_115_out, G);
  not not_116 (not_116_out, A);
  not not_117 (not_117_out, B);
  not not_118 (not_118_out, B);
  not not_119 (not_119_out, F);
  not not_120 (not_120_out, G);
  not not_121 (not_121_out, A);
  not not_122 (not_122_out, B);
  not not_123 (not_123_out, C);
  not not_124 (not_124_out, E);
  not not_125 (not_125_out, F);
  not not_126 (not_126_out, G);
  not not_127 (not_127_out, A);
  not not_128 (not_128_out, C);
  not not_129 (not_129_out, A);
  not not_130 (not_130_out, D);
  not not_131 (not_131_out, E);
  not not_132 (not_132_out, A);
  not not_133 (not_133_out, D);
  not not_134 (not_134_out, F);
  not not_135 (not_135_out, A);
  not not_136 (not_136_out, D);
  not not_137 (not_137_out, G);
  not not_138 (not_138_out, C);
  not not_139 (not_139_out, D);
  not not_140 (not_140_out, B);
  not not_141 (not_141_out, C);
  not not_142 (not_142_out, B);
  not not_143 (not_143_out, B);
  not not_144 (not_144_out, B);
  not not_145 (not_145_out, D);
  not not_146 (not_146_out, E);
  not not_147 (not_147_out, C);
  not not_148 (not_148_out, D);
  not not_149 (not_149_out, A);
  not not_150 (not_150_out, B);
  not not_151 (not_151_out, C);
  not not_152 (not_152_out, D);
  not not_153 (not_153_out, F);
  not not_154 (not_154_out, G);
  not not_155 (not_155_out, A);
  not not_156 (not_156_out, C);
  not not_157 (not_157_out, D);
  not not_158 (not_158_out, E);
  not not_159 (not_159_out, F);
  not not_160 (not_160_out, B);
  not not_161 (not_161_out, C);
  not not_162 (not_162_out, D);
  not not_163 (not_163_out, E);
  not not_164 (not_164_out, F);
  not not_165 (not_165_out, G);
  not not_166 (not_166_out, A);
  not not_167 (not_167_out, B);
  not not_168 (not_168_out, C);
  not not_169 (not_169_out, E);
  not not_170 (not_170_out, A);
  not not_171 (not_171_out, C);
  not not_172 (not_172_out, E);
  not not_173 (not_173_out, G);
  not not_174 (not_174_out, A);
  not not_175 (not_175_out, B);
  not not_176 (not_176_out, C);
  not not_177 (not_177_out, F);
  not not_178 (not_178_out, A);
  not not_179 (not_179_out, B);
  not not_180 (not_180_out, C);
  not not_181 (not_181_out, G);
  not not_182 (not_182_out, A);
  not not_183 (not_183_out, A);
  not not_184 (not_184_out, C);
  not not_185 (not_185_out, E);
  not not_186 (not_186_out, A);
  not not_187 (not_187_out, C);
  not not_188 (not_188_out, F);
  not not_189 (not_189_out, G);
  not not_190 (not_190_out, C);
  not not_191 (not_191_out, E);
  not not_192 (not_192_out, F);
  not not_193 (not_193_out, G);
  not not_194 (not_194_out, A);
  not not_195 (not_195_out, D);
  not not_196 (not_196_out, E);
  not not_197 (not_197_out, A);
  not not_198 (not_198_out, F);
  not not_199 (not_199_out, A);
  not not_200 (not_200_out, G);
  not not_201 (not_201_out, B);
  not not_202 (not_202_out, D);
  not not_203 (not_203_out, F);
  not not_204 (not_204_out, G);
  not not_205 (not_205_out, D);
  not not_206 (not_206_out, E);
  not not_207 (not_207_out, F);
  not not_208 (not_208_out, D);
  not not_209 (not_209_out, E);
  not not_210 (not_210_out, G);
  not not_211 (not_211_out, B);
  not not_212 (not_212_out, E);
  not not_213 (not_213_out, B);
  not not_214 (not_214_out, F);
  not not_215 (not_215_out, B);
  not not_216 (not_216_out, G);
  not not_217 (not_217_out, C);
  not not_218 (not_218_out, D);
  not not_219 (not_219_out, C);
  not not_220 (not_220_out, B);
  not not_221 (not_221_out, C);
  not not_222 (not_222_out, D);
  not not_223 (not_223_out, B);
  not not_224 (not_224_out, C);
  not not_225 (not_225_out, E);
  not not_226 (not_226_out, F);
  not not_227 (not_227_out, B);
  not not_228 (not_228_out, C);
  not not_229 (not_229_out, E);
  not not_230 (not_230_out, G);
  not not_231 (not_231_out, C);
  not not_232 (not_232_out, D);
  not not_233 (not_233_out, D);
  not not_234 (not_234_out, D);
  not not_235 (not_235_out, A);
  not not_236 (not_236_out, C);
  not not_237 (not_237_out, E);
  not not_238 (not_238_out, F);
  not not_239 (not_239_out, G);
  not not_240 (not_240_out, A);
  not not_241 (not_241_out, D);
  not not_242 (not_242_out, D);
  not not_243 (not_243_out, A);
  not not_244 (not_244_out, E);
  not not_245 (not_245_out, F);
  not not_246 (not_246_out, G);
  not not_247 (not_247_out, B);
  not not_248 (not_248_out, C);
  not not_249 (not_249_out, A);
  not not_250 (not_250_out, D);
  not not_251 (not_251_out, A);
  not not_252 (not_252_out, E);
  not not_253 (not_253_out, F);
  not not_254 (not_254_out, C);
  not not_255 (not_255_out, D);
  not not_256 (not_256_out, D);
  not not_257 (not_257_out, D);
  not not_258 (not_258_out, B);
  not not_259 (not_259_out, B);
  not not_260 (not_260_out, A);
  not not_261 (not_261_out, C);
  not not_262 (not_262_out, A);
  not not_263 (not_263_out, E);
  not not_264 (not_264_out, C);
  not not_265 (not_265_out, D);
  not not_266 (not_266_out, B);
  not not_267 (not_267_out, F);
  not not_268 (not_268_out, E);
  and and_1 (and_1_out, not_1_out, not_2_out, not_3_out, not_4_out);
  and and_2 (and_2_out, not_5_out, not_6_out);
  and and_3 (and_3_out, not_7_out, not_8_out, not_9_out, F);
  and and_4 (and_4_out, not_10_out, not_11_out, F, G);
  and and_5 (and_5_out, not_12_out, D, E);
  and and_6 (and_6_out, D, E, F);
  and and_7 (and_7_out, not_13_out, C, not_14_out, G);
  and and_8 (and_8_out, C, D, E, G);
  and and_9 (and_9_out, not_15_out, B, not_16_out);
  and and_10 (and_10_out, B, not_17_out, not_18_out, not_19_out, not_20_out);
  and and_11 (and_11_out, B, not_21_out, not_22_out);
  and and_12 (and_12_out, not_23_out, B, E, not_24_out);
  and and_13 (and_13_out, A, not_25_out, not_26_out);
  and and_14 (and_14_out, A, not_27_out, C);
  and and_15 (and_15_out, A, B, not_28_out);
  and and_16 (and_16_out, not_29_out, D, F);
  and and_17 (and_17_out, not_30_out, D, E);
  and and_18 (and_18_out, not_31_out, D, E);
  and and_19 (and_19_out, D, E, F);
  and and_20 (and_20_out, not_32_out, not_33_out, C);
  and and_21 (and_21_out, B, not_34_out, not_35_out, not_36_out, not_37_out);
  and and_22 (and_22_out, B, not_38_out, not_39_out, not_40_out);
  and and_23 (and_23_out, not_41_out, B, not_42_out, D);
  and and_24 (and_24_out, A, not_43_out, not_44_out);
  and and_25 (and_25_out, A, not_45_out, not_46_out, not_47_out, not_48_out);
  and and_26 (and_26_out, A, not_49_out, not_50_out);
  and and_27 (and_27_out, A, B, C);
  and and_28 (and_28_out, not_51_out, not_52_out, not_53_out, not_54_out, not_55_out);
  and and_29 (and_29_out, not_56_out, not_57_out, not_58_out);
  and and_30 (and_30_out, not_59_out, not_60_out, not_61_out);
  and and_31 (and_31_out, not_62_out, not_63_out, not_64_out);
  and and_32 (and_32_out, not_65_out, not_66_out, not_67_out, F);
  and and_33 (and_33_out, not_68_out, not_69_out, F, G);
  and and_34 (and_34_out, not_70_out, D, E);
  and and_35 (and_35_out, D, E, F);
  and and_36 (and_36_out, C, not_71_out, not_72_out);
  and and_37 (and_37_out, not_73_out, not_74_out, C, not_75_out, G);
  and and_38 (and_38_out, not_76_out, C, not_77_out, F);
  and and_39 (and_39_out, C, D, E, G);
  and and_40 (and_40_out, B, not_78_out, not_79_out, not_80_out, not_81_out);
  and and_41 (and_41_out, not_82_out, B, not_83_out, D);
  and and_42 (and_42_out, B, C, not_84_out, not_85_out);
  and and_43 (and_43_out, not_86_out, B, C, E, not_87_out);
  and and_44 (and_44_out, A, not_88_out, not_89_out, not_90_out);
  and and_45 (and_45_out, A, not_91_out, not_92_out, not_93_out);
  and and_46 (and_46_out, A, B, not_94_out);
  and and_47 (and_47_out, not_95_out, not_96_out, not_97_out, not_98_out, not_99_out);
  and and_48 (and_48_out, not_100_out, not_101_out, not_102_out, not_103_out, not_104_out, not_105_out);
  and and_49 (and_49_out, not_106_out, not_107_out, not_108_out, not_109_out, not_110_out);
  and and_50 (and_50_out, not_111_out, not_112_out, not_113_out, not_114_out, not_115_out);
  and and_51 (and_51_out, not_116_out, not_117_out, C, E);
  and and_52 (and_52_out, not_118_out, C, E, not_119_out, not_120_out);
  and and_53 (and_53_out, not_121_out, not_122_out, C, D);
  and and_54 (and_54_out, B, not_123_out, not_124_out, not_125_out, not_126_out);
  and and_55 (and_55_out, not_127_out, B, not_128_out, D);
  and and_56 (and_56_out, not_129_out, B, C, not_130_out, not_131_out);
  and and_57 (and_57_out, not_132_out, B, C, not_133_out, not_134_out);
  and and_58 (and_58_out, not_135_out, B, C, not_136_out, not_137_out);
  and and_59 (and_59_out, A, not_138_out, not_139_out, E, F);
  and and_60 (and_60_out, A, not_140_out, not_141_out, D);
  and and_61 (and_61_out, A, not_142_out, D, F);
  and and_62 (and_62_out, A, not_143_out, D, E);
  and and_63 (and_63_out, A, not_144_out, C, not_145_out, not_146_out);
  and and_64 (and_64_out, A, B, not_147_out, not_148_out);
  and and_65 (and_65_out, A, B, C, D);
  and and_66 (and_66_out, not_149_out, not_150_out, not_151_out, not_152_out, not_153_out, not_154_out);
  and and_67 (and_67_out, not_155_out, not_156_out, not_157_out, not_158_out, not_159_out);
  and and_68 (and_68_out, not_160_out, not_161_out, not_162_out, not_163_out, not_164_out, not_165_out);
  and and_69 (and_69_out, not_166_out, not_167_out, not_168_out, not_169_out, F);
  and and_70 (and_70_out, not_170_out, not_171_out, not_172_out, F, not_173_out);
  and and_71 (and_71_out, not_174_out, not_175_out, not_176_out, D, E, not_177_out);
  and and_72 (and_72_out, not_178_out, not_179_out, not_180_out, D, E, not_181_out);
  and and_73 (and_73_out, not_182_out, C, D, E, F);
  and and_74 (and_74_out, not_183_out, B, not_184_out, D, not_185_out);
  and and_75 (and_75_out, not_186_out, B, not_187_out, D, not_188_out, not_189_out);
  and and_76 (and_76_out, B, not_190_out, D, not_191_out, not_192_out, not_193_out);
  and and_77 (and_77_out, not_194_out, B, C, not_195_out, not_196_out, F);
  and and_78 (and_78_out, not_197_out, B, C, E, not_198_out);
  and and_79 (and_79_out, not_199_out, B, C, E, not_200_out);
  and and_80 (and_80_out, A, not_201_out, C, not_202_out, not_203_out, not_204_out);
  and and_81 (and_81_out, A, C, not_205_out, not_206_out, not_207_out);
  and and_82 (and_82_out, A, C, not_208_out, not_209_out, not_210_out);
  and and_83 (and_83_out, A, not_211_out, C, not_212_out, F);
  and and_84 (and_84_out, A, not_213_out, C, D, E, not_214_out);
  and and_85 (and_85_out, A, not_215_out, C, D, E, not_216_out);
  and and_86 (and_86_out, A, B, not_217_out, not_218_out, E);
  and and_87 (and_87_out, A, B, not_219_out, E, F);
  and and_88 (and_88_out, not_220_out, not_221_out, not_222_out);
  and and_89 (and_89_out, not_223_out, not_224_out, not_225_out, not_226_out);
  and and_90 (and_90_out, not_227_out, not_228_out, not_229_out, not_230_out);
  and and_91 (and_91_out, not_231_out, not_232_out, F, G);
  and and_92 (and_92_out, not_233_out, E, G);
  and and_93 (and_93_out, not_234_out, E, F);
  and and_94 (and_94_out, not_235_out, not_236_out, D);
  and and_95 (and_95_out, D, not_237_out, not_238_out, not_239_out);
  and and_96 (and_96_out, not_240_out, C, not_241_out);
  and and_97 (and_97_out, B, not_242_out, E);
  and and_98 (and_98_out, not_243_out, B, D);
  and and_99 (and_99_out, B, C, not_244_out);
  and and_100 (and_100_out, B, C, not_245_out, not_246_out);
  and and_101 (and_101_out, A, not_247_out, C, D);
  and and_102 (and_102_out, A, B, not_248_out);
  and and_103 (and_103_out, not_249_out, not_250_out);
  and and_104 (and_104_out, not_251_out, not_252_out, not_253_out);
  and and_105 (and_105_out, not_254_out, not_255_out, G);
  and and_106 (and_106_out, not_256_out, F, G);
  and and_107 (and_107_out, not_257_out, E);
  and and_108 (and_108_out, not_258_out, E, F, G);
  and and_109 (and_109_out, not_259_out, C);
  and and_110 (and_110_out, not_260_out, B, not_261_out);
  and and_111 (and_111_out, not_262_out, B, not_263_out);
  and and_112 (and_112_out, B, not_264_out, not_265_out);
  and and_113 (and_113_out, A, not_266_out, F);
  and and_114 (and_114_out, A, E, not_267_out);
  and and_115 (and_115_out, A, D, not_268_out);
  and and_116 (and_116_out, A, C, D);
  or or_1 (Top, and_1_out, and_2_out, and_3_out, and_4_out, and_5_out, and_6_out, and_7_out, and_8_out, and_9_out, and_10_out, and_11_out, and_12_out, and_13_out, and_14_out, and_15_out);
  or or_2 (Middle, and_16_out, and_17_out, and_18_out, and_19_out, and_20_out, and_21_out, and_22_out, and_23_out, and_24_out, and_25_out, and_26_out, and_27_out);
  or or_3 (Bottom, and_28_out, and_29_out, and_30_out, and_31_out, and_32_out, and_33_out, and_34_out, and_35_out, and_36_out, and_37_out, and_38_out, and_39_out, and_40_out, and_41_out, and_42_out, and_43_out, and_44_out, and_45_out, and_46_out);
  or or_4 (RightTop, and_88_out, and_89_out, and_90_out, and_91_out, and_92_out, and_93_out, and_94_out, and_95_out, and_96_out, and_97_out, and_98_out, and_99_out, and_100_out, and_101_out, and_102_out);
  or or_5 (RightBottom, and_103_out, and_104_out, and_105_out, and_106_out, and_107_out, and_108_out, and_109_out, and_110_out, and_111_out, and_112_out, and_113_out, and_114_out, and_115_out, and_116_out);
  or or_6 (LeftTop, and_47_out, and_48_out, and_49_out, and_50_out, and_51_out, and_52_out, and_53_out, and_54_out, and_55_out, and_56_out, and_57_out, and_58_out, and_59_out, and_60_out, and_61_out, and_62_out, and_63_out, and_64_out, and_65_out);
  or or_7 (LeftBottom, and_66_out, and_67_out, and_68_out, and_69_out, and_70_out, and_71_out, and_72_out, and_73_out, and_74_out, and_75_out, and_76_out, and_77_out, and_78_out, and_79_out, and_80_out, and_81_out, and_82_out, and_83_out, and_84_out, and_85_out, and_86_out, and_87_out);
endmodule

// Display 1
module _1_Display (
  input  A,
  input  B,
  input  C,
  input  D,
  input  E,
  input  F,
  output Top,
  output Middle,
  output Bottom,
  output LeftTop,
  output LeftBottom,
  output RightTop,
  output RightBottom
);

  wire and_1_out, and_2_out, and_3_out, and_4_out, and_5_out, and_6_out, and_7_out, and_8_out, and_9_out,
       and_10_out, and_11_out, and_12_out, and_13_out, and_14_out, and_15_out, and_16_out, and_17_out,
       and_18_out, and_19_out, and_20_out, and_21_out, and_22_out, and_23_out, and_24_out, and_25_out,
       not_1_out, not_2_out, not_3_out, not_4_out, not_5_out, not_6_out, not_7_out, not_8_out, not_9_out,
       not_10_out, not_11_out, not_12_out, not_13_out, not_14_out, not_15_out, not_16_out, not_17_out,
       not_18_out, not_19_out, not_20_out, not_21_out, not_22_out, not_23_out, not_24_out, not_25_out,
       not_26_out, not_27_out, not_28_out, not_29_out, not_30_out, not_31_out, not_32_out, not_33_out,
       not_34_out, not_35_out, not_36_out, not_37_out, not_38_out, not_39_out, not_40_out, not_41_out,
       not_42_out, not_43_out;

  not not_1 (not_1_out, A);
  not not_2 (not_2_out, B);
  not not_3 (not_3_out, A);
  not not_4 (not_4_out, C);
  not not_5 (not_5_out, A);
  not not_6 (not_6_out, D);
  not not_7 (not_7_out, E);
  not not_8 (not_8_out, F);
  not not_9 (not_9_out, C);
  not not_10 (not_10_out, C);
  and and_1 (and_1_out, A, B, E);
  and and_2 (and_2_out, A, B, D);
  and and_3 (and_3_out, A, B, C);
  not not_11 (not_11_out, A);
  not not_12 (not_12_out, B);
  not not_13 (not_13_out, A);
  not not_14 (not_14_out, C);
  not not_15 (not_15_out, A);
  not not_16 (not_16_out, D);
  not not_17 (not_17_out, E);
  not not_18 (not_18_out, F);
  not not_19 (not_19_out, C);
  not not_20 (not_20_out, C);
  not not_21 (not_21_out, A);
  not not_22 (not_22_out, B);
  not not_23 (not_23_out, A);
  not not_24 (not_24_out, C);
  not not_25 (not_25_out, A);
  not not_26 (not_26_out, D);
  not not_27 (not_27_out, E);
  not not_28 (not_28_out, F);
  not not_29 (not_29_out, A);
  not not_30 (not_30_out, B);
  not not_31 (not_31_out, A);
  not not_32 (not_32_out, C);
  not not_33 (not_33_out, A);
  not not_34 (not_34_out, D);
  not not_35 (not_35_out, E);
  not not_36 (not_36_out, F);
  not not_37 (not_37_out, C);
  not not_38 (not_38_out, C);
  not not_39 (not_39_out, A);
  not not_40 (not_40_out, B);
  not not_41 (not_41_out, C);
  not not_42 (not_42_out, D);
  and and_4 (and_4_out, not_41_out, not_42_out, not_43_out);
  not not_43 (not_43_out, E);
  and and_5 (and_5_out, not_1_out, not_2_out);
  and and_6 (and_6_out, not_3_out, not_4_out);
  and and_7 (and_7_out, not_5_out, not_6_out, not_7_out, not_8_out);
  and and_8 (and_8_out, B, not_9_out, E);
  and and_9 (and_9_out, B, not_10_out, D);
  and and_10 (and_10_out, A, B, C);
  or or_1 (Middle, and_1_out, and_2_out, and_3_out);
  and and_11 (and_11_out, not_11_out, not_12_out);
  and and_12 (and_12_out, not_13_out, not_14_out);
  and and_13 (and_13_out, not_15_out, not_16_out, not_17_out, not_18_out);
  and and_14 (and_14_out, B, not_19_out, E);
  and and_15 (and_15_out, B, not_20_out, D);
  and and_16 (and_16_out, A, B, C);
  and and_17 (and_17_out, not_21_out, not_22_out);
  and and_18 (and_18_out, not_23_out, not_24_out);
  or or_2 (LeftTop, and_17_out, and_18_out, and_19_out);
  and and_19 (and_19_out, not_25_out, not_26_out, not_27_out, not_28_out);
  and and_20 (and_20_out, not_29_out, not_30_out);
  and and_21 (and_21_out, not_31_out, not_32_out);
  and and_22 (and_22_out, not_33_out, not_34_out, not_35_out, not_36_out);
  and and_23 (and_23_out, B, not_37_out, E);
  and and_24 (and_24_out, B, not_38_out, D);
  and and_25 (and_25_out, A, B, C);
  or or_3 (RightBottom, not_39_out, not_40_out, and_4_out);
  or or_4 (Top, and_5_out, and_6_out, and_7_out, and_8_out, and_9_out, and_10_out);
  or or_5 (Bottom, and_11_out, and_12_out, and_13_out, and_14_out, and_15_out, and_16_out);
  or or_6 (LeftBottom, and_20_out, and_21_out, and_22_out, and_23_out, and_24_out, and_25_out);

  assign RightTop = 1'b1;
endmodule

module Input (
  input  _0,
  input  _8,
  input  _1,
  input  _9,
  input  _2,
  input  A,
  input  _3,
  input  B,
  input  _4,
  input  C,
  input  _5,
  input  D,
  input  _6,
  input  E,
  input  _7,
  input  F,
  input  Delete_input,
  output Button_state,
  output Delete_output,
  output [3:0] Input_number
);

  wire and_1_out, and_2_out, and_3_out, and_4_out, and_5_out, and_6_out, and_7_out, and_8_out, and_9_out,
       and_10_out, and_11_out, and_12_out, and_13_out, and_14_out, and_15_out, and_16_out, or_1_out, or_3_out;

  assign Input_number = _0 ? 4'b0000 : 4'bz;  // Controlled_Buffer controlled_buffer_1
  assign Input_number = _1 ? 4'b0001 : 4'bz;  // Controlled_Buffer controlled_buffer_2
  assign Input_number = _2 ? 4'b0010 : 4'bz;  // Controlled_Buffer controlled_buffer_3
  assign Input_number = _3 ? 4'b0011 : 4'bz;  // Controlled_Buffer controlled_buffer_4
  assign Input_number = _4 ? 4'b0100 : 4'bz;  // Controlled_Buffer controlled_buffer_5
  assign Input_number = _5 ? 4'b0101 : 4'bz;  // Controlled_Buffer controlled_buffer_6
  assign Input_number = _6 ? 4'b0110 : 4'bz;  // Controlled_Buffer controlled_buffer_7
  assign Input_number = _7 ? 4'b0111 : 4'bz;  // Controlled_Buffer controlled_buffer_8
  and and_1 (and_1_out, _0, 1'b1);
  and and_2 (and_2_out, _1, 1'b1);
  and and_3 (and_3_out, _2, 1'b1);
  and and_4 (and_4_out, _3, 1'b1);
  and and_5 (and_5_out, _4, 1'b1);
  and and_6 (and_6_out, _5, 1'b1);
  and and_7 (and_7_out, _6, 1'b1);
  and and_8 (and_8_out, _7, 1'b1);
  or or_1 (or_1_out, and_1_out, and_2_out, and_3_out, and_4_out, and_5_out, and_6_out, and_7_out, and_8_out);
  or or_2 (Button_state, or_1_out, or_3_out);
  or or_3 (or_3_out, and_9_out, and_10_out, and_11_out, and_12_out, and_13_out, and_14_out, and_15_out, and_16_out);
  and and_9 (and_9_out, _8, 1'b1);
  and and_10 (and_10_out, _9, 1'b1);
  and and_11 (and_11_out, A, 1'b1);
  and and_12 (and_12_out, B, 1'b1);
  and and_13 (and_13_out, C, 1'b1);
  and and_14 (and_14_out, D, 1'b1);
  and and_15 (and_15_out, E, 1'b1);
  and and_16 (and_16_out, F, 1'b1);
  assign Input_number = _8 ? 4'b1000 : 4'bz;  // Controlled_Buffer controlled_buffer_9
  assign Input_number = _9 ? 4'b1001 : 4'bz;  // Controlled_Buffer controlled_buffer_10
  assign Input_number = A ? 4'b1010 : 4'bz;  // Controlled_Buffer controlled_buffer_11
  assign Input_number = B ? 4'b1011 : 4'bz;  // Controlled_Buffer controlled_buffer_12
  assign Input_number = C ? 4'b1100 : 4'bz;  // Controlled_Buffer controlled_buffer_13
  assign Input_number = D ? 4'b1101 : 4'bz;  // Controlled_Buffer controlled_buffer_14
  assign Input_number = E ? 4'b1110 : 4'bz;  // Controlled_Buffer controlled_buffer_15
  assign Input_number = F ? 4'b1111 : 4'bz;  // Controlled_Buffer controlled_buffer_16

  assign Delete_output = Delete_input;

  // Other names for the same wires on the sheet: Output[3:0] = Input_number
endmodule

module Register (
  input  [3:0] Input,
  input  Button_state,
  input  Delete_button,
  output [3:0] First_number,
  output [3:0] Second_number,
  output [7:0] Output
);

  Shift_Register #(.width(4), .length(2), .trigger("falling")) shift_register_1 (
    .shift(1'b1), .in(Input), .clk(Button_state), .load(1'b0), .clr(Delete_button), .d0(4'b0000),
    .q0(Output[3:0]), .d1(4'b0000), .q1(First_number));  // open: out

  assign Output[7:4] = First_number;
  assign Second_number = Output[3:0];
endmodule

// HEX-DEC CONVERTOR
module Convertor (
  input  _0,
  input  _1,
  input  _2,
  input  _3,
  input  _4,
  input  _5,
  input  _6,
  input  _7,
  input  _8,
  input  _9,
  input  A,
  input  B,
  input  C,
  input  D,
  input  E,
  input  F,
  input  Delete,
  output [3:0] _3_Top,
  output [2:0] _3_Bottom,
  output [3:0] _2_Top,
  output [2:0] _2_Bottom,
  output [3:0] _1_Top,
  output [2:0] _1_Bottom,
  output [3:0] First_number,
  output [3:0] Second_number
);

  wire input_1_button_state, input_1_delete_output;
  wire [3:0] input_1_input_number, \Registr_pro_uložení_hodnoty_q ;
  wire [7:0] register_1_output;

  Input input_1 (
    ._0(_0), ._1(_1), ._2(_2), ._3(_3), ._4(_4), ._5(_5), ._6(_6), ._7(_7), .Delete_input(Delete), ._8(_8),
    ._9(_9), .A(A), .B(B), .C(C), .D(D), .E(E), .F(F), .Delete_output(input_1_delete_output),
    .Input_number(input_1_input_number), .Button_state(input_1_button_state));
  Register_part #(.width(4)) \Registr_pro_uložení_hodnoty  (
    .D(input_1_input_number), .Q(\Registr_pro_uložení_hodnoty_q ), .clk(input_1_button_state),
    .clr(input_1_delete_output));  // open: en
  Register register_1 (
    .Button_state(input_1_button_state), .Delete_button(input_1_delete_output), .First_number(First_number),
    .Second_number(Second_number), .Output(register_1_output), .Input(\Registr_pro_uložení_hodnoty_q ));
  _3_Display u_3_display_1 (
    .A(register_1_output[7]), .B(register_1_output[6]), .C(register_1_output[5]), .D(register_1_output[4]),
    .E(register_1_output[3]), .F(register_1_output[2]), .G(register_1_output[1]), .H(register_1_output[0]),
    .Top(_3_Top[1]), .Middle(_3_Top[3]), .Bottom(_3_Bottom[1]), .LeftTop(_3_Top[2]),
    .LeftBottom(_3_Bottom[2]), .RightTop(_3_Top[0]), .RightBottom(_3_Bottom[0]));
  _2_Display u_2_display_1 (
    .A(register_1_output[7]), .B(register_1_output[6]), .C(register_1_output[5]), .D(register_1_output[4]),
    .E(register_1_output[3]), .F(register_1_output[2]), .G(register_1_output[1]), .Top(_2_Top[1]),
    .Middle(_2_Top[3]), .Bottom(_2_Bottom[1]), .LeftTop(_2_Top[2]), .LeftBottom(_2_Bottom[2]),
    .RightTop(_2_Top[0]), .RightBottom(_2_Bottom[0]));
  _1_Display u_1_display_1 (
    .A(register_1_output[7]), .B(register_1_output[6]), .C(register_1_output[5]), .D(register_1_output[4]),
    .E(register_1_output[3]), .F(register_1_output[2]), .Top(_1_Top[1]), .Middle(_1_Top[3]),
    .Bottom(_1_Bottom[1]), .LeftTop(_1_Top[2]), .LeftBottom(_1_Bottom[2]), .RightTop(_1_Top[0]),
    .RightBottom(_1_Bottom[0]));
endmodule
